// Logisim project F3.3.4.circ as structural Verilog: 1 circuit, main circuit main
module main (
  input  in_1,
  input  in_2,
  output Y
);

  wire and_1_out, and_3_out, not_1_out, not_2_out;

  not not_1 (not_1_out, in_1);
  not not_2 (not_2_out, in_2);
  and and_1 (and_1_out, in_1, not_2_out);
  and and_2 (and_1_out, in_1, not_2_out);
  and and_3 (and_3_out, not_1_out, in_2);
  and and_4 (and_3_out, not_1_out, in_2);
  nor nor_1 (Y, and_1_out, and_3_out);

  // Notes on the sheet:
  //   共使用了22个晶体管
  //   共使用了20个晶体管
endmodule
