// Logisim project F3.3.5.circ as structural Verilog: 1 circuit, main circuit main
module main (
  input  A,
  input  B,
  output Y
);

  wire xor_1_out;

  xor xor_1 (xor_1_out, A, B);
  not not_1 (Y, xor_1_out);

  // Notes on the sheet:
  //   6 晶体管 XNOR 门实现
  //   逻辑：Y = (A⊕B)' = A⊙B
  //   实现方式：XOR(4管) + NOT(2管) = 6管
endmodule
