// Logisim project F3.5.17.circ as structural Verilog: 1 circuit, main circuit main
module main (
);

  wire A0, A1, A2, A3, B0, B1, B2, B3, decoder_7_segment_display_1_a, decoder_7_segment_display_1_b,
       decoder_7_segment_display_1_c, decoder_7_segment_display_1_d, decoder_7_segment_display_1_e,
       decoder_7_segment_display_1_f, decoder_7_segment_display_1_g, decoder_7_segment_display_2_a,
       decoder_7_segment_display_2_b, decoder_7_segment_display_2_c, decoder_7_segment_display_2_d,
       decoder_7_segment_display_2_e, decoder_7_segment_display_2_f, decoder_7_segment_display_2_g,
       decoder_7_segment_display_3_a, decoder_7_segment_display_3_b, decoder_7_segment_display_3_c,
       decoder_7_segment_display_3_d, decoder_7_segment_display_3_e, decoder_7_segment_display_3_f,
       decoder_7_segment_display_3_g, FA0_count, FA1_count, FA2_count, FA3_count, not_1_out, not_2_out,
       not_3_out, not_4_out, not_5_out, S0, S1, S2, S3;

  // DipSwitch #(.number(4)) dipswitch_1: pin names not known; wires that end beside it: A0, A1, A2, A3
  // DipSwitch #(.number(4)) dipswitch_2: pin names not known; wires that end beside it: B0, B1, B2, B3
  Decoder_7_Segment_Display decoder_7_segment_display_1 (
    .A2(A2), .A3(A3), .A0(A0), .A1(A1), .A(decoder_7_segment_display_1_a), .B(decoder_7_segment_display_1_b),
    .E(decoder_7_segment_display_1_e), .D(decoder_7_segment_display_1_d), .C(decoder_7_segment_display_1_c),
    .G(decoder_7_segment_display_1_g), .F(decoder_7_segment_display_1_f));
  Decoder_7_Segment_Display decoder_7_segment_display_2 (
    .A2(B2), .A3(B3), .A0(B0), .A1(B1), .A(decoder_7_segment_display_2_a), .B(decoder_7_segment_display_2_b),
    .E(decoder_7_segment_display_2_e), .D(decoder_7_segment_display_2_d), .C(decoder_7_segment_display_2_c),
    .G(decoder_7_segment_display_2_g), .F(decoder_7_segment_display_2_f));
  _7_Segment_Display u_7_segment_display_1 (
    .g(decoder_7_segment_display_1_g), .f(decoder_7_segment_display_1_f), .a(decoder_7_segment_display_1_a),
    .b(decoder_7_segment_display_1_b), .e(decoder_7_segment_display_1_e), .d(decoder_7_segment_display_1_d),
    .c(decoder_7_segment_display_1_c));  // open: dp
  _7_Segment_Display u_7_segment_display_2 (
    .g(decoder_7_segment_display_2_g), .f(decoder_7_segment_display_2_f), .a(decoder_7_segment_display_2_a),
    .b(decoder_7_segment_display_2_b), .e(decoder_7_segment_display_2_e), .d(decoder_7_segment_display_2_d),
    .c(decoder_7_segment_display_2_c));  // open: dp
  not not_1 (not_1_out, B0);
  not not_2 (not_2_out, B1);
  not not_3 (not_3_out, B2);
  not not_4 (not_4_out, B3);
  Full_Adder_1bit FA0 (.A(A0), .B(not_1_out), .Cin(1'b1), .Sum(S0), .Count(FA0_count));
  Full_Adder_1bit FA1 (.A(A1), .B(not_2_out), .Cin(FA0_count), .Sum(S1), .Count(FA1_count));
  Full_Adder_1bit FA2 (.A(A2), .B(not_3_out), .Cin(FA1_count), .Sum(S2), .Count(FA2_count));
  Full_Adder_1bit FA3 (.A(A3), .B(not_4_out), .Cin(FA2_count), .Sum(S3), .Count(FA3_count));
  not not_5 (not_5_out, FA3_count);
  LED led_1 (.in(not_5_out));
  Decoder_7_Segment_Display decoder_7_segment_display_3 (
    .A2(S2), .A3(S3), .A0(S0), .A1(S1), .A(decoder_7_segment_display_3_a), .B(decoder_7_segment_display_3_b),
    .E(decoder_7_segment_display_3_e), .D(decoder_7_segment_display_3_d), .C(decoder_7_segment_display_3_c),
    .G(decoder_7_segment_display_3_g), .F(decoder_7_segment_display_3_f));
  _7_Segment_Display u_7_segment_display_3 (
    .g(decoder_7_segment_display_3_g), .f(decoder_7_segment_display_3_f), .a(decoder_7_segment_display_3_a),
    .b(decoder_7_segment_display_3_b), .e(decoder_7_segment_display_3_e), .d(decoder_7_segment_display_3_d),
    .c(decoder_7_segment_display_3_c));  // open: dp
endmodule
