// Logisim project F3.5.18.circ as structural Verilog: 1 circuit, main circuit main
module main (
);

  wire A0, A1, A2, A3, B0, B1, B2, B3, decoder_7_segment_display_1_a, decoder_7_segment_display_1_b,
       decoder_7_segment_display_1_c, decoder_7_segment_display_1_d, decoder_7_segment_display_1_e,
       decoder_7_segment_display_1_f, decoder_7_segment_display_1_g, decoder_7_segment_display_2_a,
       decoder_7_segment_display_2_b, decoder_7_segment_display_2_c, decoder_7_segment_display_2_d,
       decoder_7_segment_display_2_e, decoder_7_segment_display_2_f, decoder_7_segment_display_2_g,
       decoder_7_segment_display_3_a, decoder_7_segment_display_3_b, decoder_7_segment_display_3_c,
       decoder_7_segment_display_3_d, decoder_7_segment_display_3_e, decoder_7_segment_display_3_f,
       decoder_7_segment_display_3_g, diff, eq0, eq1, eq2, FA0_count, FA1_count, FA2_count, FA3_count, S0,
       S1, S2, S3;

  // DipSwitch #(.number(4)) dipswitch_1: pin names not known; wires that end beside it: A0, A1, A2, A3
  // DipSwitch #(.number(4)) dipswitch_2: pin names not known; wires that end beside it: B0, B1, B2, B3
  xor xor_1 (diff, A3, B3);
  xor xor_2 (eq2, A2, B2);
  xor xor_3 (eq1, A1, B2);
  xor xor_4 (eq0, A0, B0);
  Decoder_7_Segment_Display decoder_7_segment_display_1 (
    .A2(A2), .A3(A3), .A0(A0), .A1(A1), .A(decoder_7_segment_display_1_a), .B(decoder_7_segment_display_1_b),
    .E(decoder_7_segment_display_1_e), .D(decoder_7_segment_display_1_d), .C(decoder_7_segment_display_1_c),
    .G(decoder_7_segment_display_1_g), .F(decoder_7_segment_display_1_f));
  Decoder_7_Segment_Display decoder_7_segment_display_2 (
    .A2(B2), .A3(B3), .A0(B0), .A1(B1), .A(decoder_7_segment_display_2_a), .B(decoder_7_segment_display_2_b),
    .E(decoder_7_segment_display_2_e), .D(decoder_7_segment_display_2_d), .C(decoder_7_segment_display_2_c),
    .G(decoder_7_segment_display_2_g), .F(decoder_7_segment_display_2_f));
  _7_Segment_Display u_7_segment_display_1 (
    .g(decoder_7_segment_display_1_g), .f(decoder_7_segment_display_1_f), .a(decoder_7_segment_display_1_a),
    .b(decoder_7_segment_display_1_b), .e(decoder_7_segment_display_1_e), .d(decoder_7_segment_display_1_d),
    .c(decoder_7_segment_display_1_c));  // open: dp
  _7_Segment_Display u_7_segment_display_2 (
    .g(decoder_7_segment_display_2_g), .f(decoder_7_segment_display_2_f), .a(decoder_7_segment_display_2_a),
    .b(decoder_7_segment_display_2_b), .e(decoder_7_segment_display_2_e), .d(decoder_7_segment_display_2_d),
    .c(decoder_7_segment_display_2_c));  // open: dp
  Full_Adder_1bit FA0 (.A(A0), .B(B0), .Cin(1'b0), .Sum(S0), .Count(FA0_count));
  Full_Adder_1bit FA1 (.A(A1), .B(B1), .Cin(FA0_count), .Sum(S1), .Count(FA1_count));
  Full_Adder_1bit FA2 (.A(A2), .B(B2), .Cin(FA1_count), .Sum(S2), .Count(FA2_count));
  Full_Adder_1bit FA3 (.A(A3), .B(B3), .Cin(FA2_count), .Sum(S3), .Count(FA3_count));
  LED led_1 (.in(FA3_count));
  Decoder_7_Segment_Display decoder_7_segment_display_3 (
    .A2(S2), .A3(S3), .A0(S0), .A1(S1), .A(decoder_7_segment_display_3_a), .B(decoder_7_segment_display_3_b),
    .E(decoder_7_segment_display_3_e), .D(decoder_7_segment_display_3_d), .C(decoder_7_segment_display_3_c),
    .G(decoder_7_segment_display_3_g), .F(decoder_7_segment_display_3_f));
  _7_Segment_Display u_7_segment_display_3 (
    .g(decoder_7_segment_display_3_g), .f(decoder_7_segment_display_3_f), .a(decoder_7_segment_display_3_a),
    .b(decoder_7_segment_display_3_b), .e(decoder_7_segment_display_3_e), .d(decoder_7_segment_display_3_d),
    .c(decoder_7_segment_display_3_c));  // open: dp
endmodule
