// Logisim project F3.5.8.circ as structural Verilog: 1 circuit, main circuit main
module main (
);

  wire decoder_4to16_1_y0, decoder_4to16_1_y1, decoder_4to16_1_y2, decoder_4to16_1_y3, decoder_4to16_1_y4,
       decoder_4to16_1_y5, decoder_4to16_1_y6, decoder_4to16_1_y7, decoder_4to16_1_y8, decoder_4to16_1_y9,
       decoder_4to16_1_y10, decoder_4to16_1_y11, decoder_4to16_1_y12, decoder_4to16_1_y13,
       decoder_4to16_1_y14, decoder_4to16_1_y15, dipswitch_1_p1, dipswitch_1_p2, dipswitch_1_p3,
       dipswitch_1_p4, dipswitch_1_p5, dipswitch_1_p6, dipswitch_1_p7, dipswitch_1_p8, dipswitch_1_p9,
       dipswitch_1_p10, dipswitch_1_p11, dipswitch_1_p12, dipswitch_1_p13, dipswitch_1_p14, dipswitch_1_p15,
       dipswitch_1_p16, or_1_out, or_2_out, or_3_out, or_4_out, or_5_out, or_6_out, or_7_out,
       priority_encoder_16to4_1_b0, priority_encoder_16to4_1_b1, priority_encoder_16to4_1_b2,
       priority_encoder_16to4_1_b3;

  // DipSwitch #(.number(16)) dipswitch_1: pin names not known; wires that end beside it: dipswitch_1_p1, dipswitch_1_p2, dipswitch_1_p3, dipswitch_1_p4, dipswitch_1_p5, dipswitch_1_p6, dipswitch_1_p7, dipswitch_1_p8, dipswitch_1_p9, dipswitch_1_p10, dipswitch_1_p11, dipswitch_1_p12, dipswitch_1_p13, dipswitch_1_p14, dipswitch_1_p15, dipswitch_1_p16
  Priority_Encoder_16to4 priority_encoder_16to4_1 (
    .I0(dipswitch_1_p1), .I1(dipswitch_1_p2), .I2(dipswitch_1_p3), .I3(dipswitch_1_p4), .I4(dipswitch_1_p5),
    .I5(dipswitch_1_p6), .I6(dipswitch_1_p7), .I7(dipswitch_1_p8), .I8(dipswitch_1_p9), .I9(dipswitch_1_p10),
    .I10(dipswitch_1_p11), .I11(dipswitch_1_p12), .I12(dipswitch_1_p13), .I13(dipswitch_1_p14),
    .I14(dipswitch_1_p15), .I15(dipswitch_1_p16), .B0(priority_encoder_16to4_1_b0),
    .B1(priority_encoder_16to4_1_b1), .B2(priority_encoder_16to4_1_b2), .B3(priority_encoder_16to4_1_b3));
  Decoder_4to16 decoder_4to16_1 (
    .A0(priority_encoder_16to4_1_b0), .A1(priority_encoder_16to4_1_b1), .A2(priority_encoder_16to4_1_b2),
    .A3(priority_encoder_16to4_1_b3), .Y0(decoder_4to16_1_y0), .Y1(decoder_4to16_1_y1),
    .Y2(decoder_4to16_1_y2), .Y3(decoder_4to16_1_y3), .Y4(decoder_4to16_1_y4), .Y5(decoder_4to16_1_y5),
    .Y6(decoder_4to16_1_y6), .Y7(decoder_4to16_1_y7), .Y8(decoder_4to16_1_y8), .Y9(decoder_4to16_1_y9),
    .Y10(decoder_4to16_1_y10), .Y11(decoder_4to16_1_y11), .Y12(decoder_4to16_1_y12),
    .Y13(decoder_4to16_1_y13), .Y14(decoder_4to16_1_y14), .Y15(decoder_4to16_1_y15));
  or or_1 (or_1_out, decoder_4to16_1_y2, decoder_4to16_1_y3, decoder_4to16_1_y4, decoder_4to16_1_y5, decoder_4to16_1_y6, decoder_4to16_1_y8, decoder_4to16_1_y9, decoder_4to16_1_y10, decoder_4to16_1_y11, decoder_4to16_1_y13, decoder_4to16_1_y14, decoder_4to16_1_y15);
  or or_2 (or_2_out, decoder_4to16_1_y0, decoder_4to16_1_y4, decoder_4to16_1_y5, decoder_4to16_1_y6, decoder_4to16_1_y8, decoder_4to16_1_y9, decoder_4to16_1_y10, decoder_4to16_1_y11, decoder_4to16_1_y12, decoder_4to16_1_y14, decoder_4to16_1_y15);
  or or_3 (or_3_out, decoder_4to16_1_y0, decoder_4to16_1_y2, decoder_4to16_1_y3, decoder_4to16_1_y5, decoder_4to16_1_y6, decoder_4to16_1_y7, decoder_4to16_1_y8, decoder_4to16_1_y9, decoder_4to16_1_y10, decoder_4to16_1_y12, decoder_4to16_1_y14, decoder_4to16_1_y15);
  or or_4 (or_4_out, decoder_4to16_1_y0, decoder_4to16_1_y1, decoder_4to16_1_y2, decoder_4to16_1_y3, decoder_4to16_1_y4, decoder_4to16_1_y7, decoder_4to16_1_y8, decoder_4to16_1_y9, decoder_4to16_1_y10, decoder_4to16_1_y13);
  or or_5 (or_5_out, decoder_4to16_1_y0, decoder_4to16_1_y2, decoder_4to16_1_y6, decoder_4to16_1_y8, decoder_4to16_1_y10, decoder_4to16_1_y11, decoder_4to16_1_y12, decoder_4to16_1_y13, decoder_4to16_1_y14, decoder_4to16_1_y15);
  or or_6 (or_6_out, decoder_4to16_1_y0, decoder_4to16_1_y2, decoder_4to16_1_y3, decoder_4to16_1_y5, decoder_4to16_1_y6, decoder_4to16_1_y8, decoder_4to16_1_y9, decoder_4to16_1_y11, decoder_4to16_1_y12, decoder_4to16_1_y13, decoder_4to16_1_y14);
  or or_7 (or_7_out, decoder_4to16_1_y0, decoder_4to16_1_y1, decoder_4to16_1_y3, decoder_4to16_1_y4, decoder_4to16_1_y5, decoder_4to16_1_y6, decoder_4to16_1_y7, decoder_4to16_1_y8, decoder_4to16_1_y9, decoder_4to16_1_y10, decoder_4to16_1_y11, decoder_4to16_1_y13);
  _7_Segment_Display u_7_segment_display_1 (
    .g(or_1_out), .f(or_2_out), .a(or_3_out), .b(or_4_out), .e(or_5_out), .d(or_6_out), .c(or_7_out));  // open: dp
endmodule
