// Logisim project F3.5.circ as structural Verilog: 2 circuits, main circuit main
module main (
);

  Decoder_2to4 decoder_2to4_1 ();  // open: IN0, IN1, OUT0, OUT1, OUT2, OUT3
endmodule

module Decoder_2to4 (
  input  IN0,
  input  IN1,
  output OUT0,
  output OUT1,
  output OUT2,
  output OUT3
);

  wire not_1_out, not_2_out;

  not not_1 (not_1_out, IN0);
  not not_2 (not_2_out, IN1);
  and and_1 (OUT0, not_1_out, not_2_out);
  and and_2 (OUT1, IN0, not_2_out);
  and and_3 (OUT2, not_1_out, IN1);
  and and_4 (OUT3, IN0, IN1);
endmodule
