// Logisim project F3.5_library.circ as structural Verilog
module Decoder_2to4 (
  input  IN0,
  input  IN1,
  input  EN,
  output OUT0,
  output OUT1,
  output OUT2,
  output OUT3
);

  wire not_1_out, not_2_out;

  not not_1 (not_1_out, IN0);
  not not_2 (not_2_out, IN1);
  and and_1 (OUT0, not_1_out, EN, not_2_out);
  and and_2 (OUT1, IN0, EN, not_2_out);
  and and_3 (OUT2, not_1_out, EN, IN1);
  and and_4 (OUT3, IN0, EN, IN1);
endmodule

module Decoder_3to8 (
  input  A0,
  input  A1,
  input  A2,
  input  EN,
  output Y0,
  output Y1,
  output Y2,
  output Y3,
  output Y4,
  output Y5,
  output Y6,
  output Y7
);

  wire decoder_2to4_1_out0, decoder_2to4_1_out1, decoder_2to4_1_out2, decoder_2to4_1_out3,
       decoder_2to4_2_out0, decoder_2to4_2_out1, decoder_2to4_2_out2, decoder_2to4_2_out3, not_1_out;

  not not_1 (not_1_out, A2);
  Decoder_2to4 decoder_2to4_1 (
    .IN0(A0), .IN1(A1), .EN(not_1_out), .OUT0(decoder_2to4_1_out0), .OUT1(decoder_2to4_1_out1),
    .OUT2(decoder_2to4_1_out2), .OUT3(decoder_2to4_1_out3));
  Decoder_2to4 decoder_2to4_2 (
    .IN0(A0), .IN1(A1), .EN(A2), .OUT0(decoder_2to4_2_out0), .OUT1(decoder_2to4_2_out1),
    .OUT2(decoder_2to4_2_out2), .OUT3(decoder_2to4_2_out3));
  and and_1 (Y0, decoder_2to4_1_out0, EN);
  and and_2 (Y1, decoder_2to4_1_out1, EN);
  and and_3 (Y2, decoder_2to4_1_out2, EN);
  and and_4 (Y3, decoder_2to4_1_out3, EN);
  and and_5 (Y4, decoder_2to4_2_out0, EN);
  and and_6 (Y5, decoder_2to4_2_out1, EN);
  and and_7 (Y6, decoder_2to4_2_out2, EN);
  and and_8 (Y7, decoder_2to4_2_out3, EN);
endmodule

module Decoder_4to16 (
  input  A0,
  input  A1,
  input  A2,
  input  A3,
  output Y0,
  output Y1,
  output Y2,
  output Y3,
  output Y4,
  output Y5,
  output Y6,
  output Y7,
  output Y8,
  output Y9,
  output Y10,
  output Y11,
  output Y12,
  output Y13,
  output Y14,
  output Y15
);

  wire not_1_out;

  not not_1 (not_1_out, A3);
  Decoder_3to8 decoder_3to8_1 (
    .A0(A0), .A1(A1), .A2(A2), .EN(not_1_out), .Y0(Y0), .Y1(Y1), .Y2(Y2), .Y3(Y3), .Y4(Y4), .Y5(Y5), .Y6(Y6),
    .Y7(Y7));
  Decoder_3to8 decoder_3to8_2 (
    .A0(A0), .A1(A1), .A2(A2), .EN(A3), .Y0(Y8), .Y1(Y9), .Y2(Y10), .Y3(Y11), .Y4(Y12), .Y5(Y13), .Y6(Y14),
    .Y7(Y15));
endmodule

module Encoder_16to4 (
  input  I0,
  input  I1,
  input  I2,
  input  I3,
  input  I4,
  input  I5,
  input  I6,
  input  I7,
  input  I8,
  input  I9,
  input  I10,
  input  I11,
  input  I12,
  input  I13,
  input  I14,
  input  I15,
  output B0_LSB,
  output B1,
  output B2,
  output B3_MSB
);

  or or_1 (B0_LSB, I1, I3, I5, I7, I9, I11, I13, I15);
  or or_2 (B1, I2, I3, I6, I7, I10, I11, I14, I15);
  or or_3 (B2, I4, I5, I6, I7, I12, I13, I14, I15);
  or or_4 (B3_MSB, I8, I9, I10, I11, I12, I13, I14, I15);
endmodule

module Priority_Encoder_4to2 (
  input  I0,
  input  I1,
  input  I2,
  input  I3,
  output Y0,
  output Y1
);

  wire and_1_out, not_1_out;

  not not_1 (not_1_out, I2);
  and and_1 (and_1_out, I1, not_1_out);
  or or_1 (Y0, and_1_out, I3);
  or or_2 (Y1, I2, I3);
endmodule

module Priority_Encoder_16to4 (
  input  I0,
  input  I1,
  input  I2,
  input  I3,
  input  I4,
  input  I5,
  input  I6,
  input  I7,
  input  I8,
  input  I9,
  input  I10,
  input  I11,
  input  I12,
  input  I13,
  input  I14,
  input  I15,
  output B0,
  output B1,
  output B2,
  output B3
);

  wire and_1_out, and_2_out, and_3_out, and_4_out, and_5_out, and_6_out, and_7_out, e0_0, e0_1, e1_0, e1_1,
       e2_0, e2_1, e3_0, e3_1, V0, V1, V2;

  Priority_Encoder_4to2 E0 (.I0(I0), .I1(I1), .I2(I2), .I3(I3), .Y0(e0_0), .Y1(e0_1));
  Priority_Encoder_4to2 E1 (.I0(I4), .I1(I5), .I2(I6), .I3(I7), .Y0(e1_0), .Y1(e1_1));
  Priority_Encoder_4to2 E2 (.I0(I8), .I1(I9), .I2(I10), .I3(I11), .Y0(e2_0), .Y1(e2_1));
  Priority_Encoder_4to2 E3 (.I0(I12), .I1(I13), .I2(I14), .I3(I15), .Y0(e3_0), .Y1(e3_1));
  or or_1 (V0, I0, I1, I2, I3);
  or or_2 (V1, I4, I5, I6, I7);
  or or_3 (V2, I8, I9, I10, I11);
  or or_4 (B3, I12, I13, I14, I15);
  and and_1 (and_1_out, e3_0, B3);
  and and_2 (and_2_out, e2_0, V2);
  and and_3 (and_3_out, e1_0, V1);
  and and_4 (and_4_out, e0_0, V0);
  and and_5 (and_5_out, e3_1, B3);
  and and_6 (and_6_out, e2_1, V2);
  and and_7 (and_7_out, e1_1, V1);
  or or_5 (B1, and_5_out, and_6_out, and_7_out);
  or or_6 (B0, and_1_out, and_2_out, and_3_out, and_4_out);
  or or_7 (B2, V2, B3);

  // Other names for the same wires on the sheet: V3 = B3
endmodule

module MUX_2to1 (
  input  A,
  input  B,
  input  S,
  output Y
);

  wire and_1_out, and_2_out, not_1_out;

  not not_1 (not_1_out, S);
  and and_1 (and_1_out, A, not_1_out);
  and and_2 (and_2_out, B, S);
  or or_1 (Y, and_1_out, and_2_out);
endmodule

module MUX_4to1 (
  input  A,
  input  B,
  input  C,
  input  D,
  input  S0,
  input  S1,
  output Y
);

  wire mux_2to1_1_y, mux_2to1_2_y;

  MUX_2to1 mux_2to1_1 (.A(A), .B(B), .S(S0), .Y(mux_2to1_1_y));
  MUX_2to1 mux_2to1_2 (.A(C), .B(D), .S(S0), .Y(mux_2to1_2_y));
  MUX_2to1 mux_2to1_3 (.A(mux_2to1_1_y), .B(mux_2to1_2_y), .S(S1), .Y(Y));
endmodule

module MUX_4to1_3bit (
  input  A0,
  input  B0,
  input  C0,
  input  D0,
  input  A1,
  input  B1,
  input  C1,
  input  D1,
  input  A2,
  input  B2,
  input  C2,
  input  D2,
  input  S0,
  input  S1,
  output Y0,
  output Y1,
  output Y2
);

  MUX_4to1 mux_4to1_1 (.A(A0), .B(B0), .C(C0), .D(D0), .S0(S0), .S1(S1), .Y(Y0));
  MUX_4to1 mux_4to1_2 (.A(A1), .B(B1), .C(C1), .D(D1), .S0(S0), .S1(S1), .Y(Y1));
  MUX_4to1 mux_4to1_3 (.A(A2), .B(B2), .C(C2), .D(D2), .S0(S0), .S1(S1), .Y(Y2));
endmodule

module Comparator_4bit (
  input  A0,
  input  B0,
  input  A1,
  input  B1,
  input  A2,
  input  B2,
  input  A3,
  input  B3,
  output Y
);

  wire xnor_1_out, xnor_2_out, xnor_3_out, xnor_4_out;

  xnor xnor_1 (xnor_1_out, A0, B0);
  xnor xnor_2 (xnor_2_out, A1, B1);
  xnor xnor_3 (xnor_3_out, A2, B2);
  xnor xnor_4 (xnor_4_out, A3, B3);
  and and_1 (Y, xnor_1_out, xnor_2_out, xnor_3_out, xnor_4_out);
endmodule

module Full_Adder_1bit (
  input  A,
  input  B,
  input  Cin,
  output Sum,
  output Count
);

  wire half_adder_1bit_1_cout, half_adder_1bit_1_sum, half_adder_1bit_2_cout;

  Half_Adder_1bit half_adder_1bit_1 (.A(A), .B(B), .sum(half_adder_1bit_1_sum), .cout(half_adder_1bit_1_cout));
  Half_Adder_1bit half_adder_1bit_2 (.A(half_adder_1bit_1_sum), .B(Cin), .sum(Sum), .cout(half_adder_1bit_2_cout));
  or or_1 (Count, half_adder_1bit_2_cout, half_adder_1bit_1_cout);
endmodule

module Half_Adder_1bit (
  input  A,
  input  B,
  output sum,
  output cout
);

  xor xor_1 (sum, A, B);
  and and_1 (cout, A, B);
endmodule

module Decoder_7_Segment_Display (
  input  A0,
  input  A1,
  input  A2,
  input  A3,
  output G,
  output F,
  output A,
  output B,
  output E,
  output D,
  output C
);

  wire and_1_out, and_2_out, and_3_out, and_4_out, and_5_out, and_6_out, and_7_out, and_8_out, and_9_out,
       and_10_out, and_11_out, and_12_out, and_13_out, and_14_out, and_15_out, and_16_out, and_17_out,
       and_18_out, and_19_out, and_20_out, and_21_out, and_22_out, and_23_out, and_24_out, and_25_out,
       and_26_out, and_27_out, and_28_out, and_29_out, and_30_out, and_31_out, and_32_out, and_33_out,
       and_34_out, and_35_out, not_1_out, not_2_out, not_3_out, not_4_out;

  not not_1 (not_1_out, A0);
  not not_2 (not_2_out, A1);
  not not_3 (not_3_out, A2);
  not not_4 (not_4_out, A3);
  and and_1 (and_1_out, not_3_out, A3);
  and and_2 (and_2_out, A1, not_3_out);
  and and_3 (and_3_out, not_1_out, A1);
  and and_4 (and_4_out, not_2_out, A2, not_4_out);
  and and_5 (and_5_out, A0, A3);
  and and_6 (and_6_out, not_1_out, not_2_out);
  and and_7 (and_7_out, not_1_out, A2);
  and and_8 (and_8_out, not_3_out, A3);
  and and_9 (and_9_out, not_2_out, A2, not_4_out);
  and and_10 (and_10_out, A1, A3);
  and and_11 (and_11_out, not_1_out, not_3_out);
  and and_12 (and_12_out, not_1_out, A3);
  and and_13 (and_13_out, not_2_out, not_3_out, A3);
  and and_14 (and_14_out, A0, A2, not_4_out);
  and and_15 (and_15_out, A1, not_4_out);
  and and_16 (and_16_out, A1, A2);
  and and_17 (and_17_out, not_1_out, not_2_out, not_4_out);
  and and_18 (and_18_out, not_1_out, not_3_out);
  and and_19 (and_19_out, A0, not_2_out, A3);
  and and_20 (and_20_out, A0, A1, not_4_out);
  and and_21 (and_21_out, not_2_out, not_3_out);
  and and_22 (and_22_out, not_1_out, not_3_out);
  and and_23 (and_23_out, not_1_out, A1);
  and and_24 (and_24_out, A2, A3);
  and and_25 (and_25_out, A1, A3);
  and and_26 (and_26_out, A0, not_2_out, A2);
  and and_27 (and_27_out, not_1_out, not_3_out, not_4_out);
  and and_28 (and_28_out, not_1_out, A1, A2);
  and and_29 (and_29_out, not_2_out, A3);
  and and_30 (and_30_out, A0, A1, not_3_out);
  and and_31 (and_31_out, not_3_out, A3);
  and and_32 (and_32_out, A2, not_4_out);
  and and_33 (and_33_out, A0, not_2_out);
  and and_34 (and_34_out, not_2_out, not_3_out);
  and and_35 (and_35_out, A0, not_3_out);
  or or_1 (G, and_1_out, and_2_out, and_3_out, and_4_out, and_5_out);
  or or_2 (F, and_6_out, and_7_out, and_8_out, and_9_out, and_10_out);
  or or_3 (A, and_11_out, and_12_out, and_13_out, and_14_out, and_15_out, and_16_out);
  or or_4 (B, and_17_out, and_18_out, and_19_out, and_20_out, and_21_out);
  or or_5 (E, and_22_out, and_23_out, and_24_out, and_25_out);
  or or_6 (D, and_26_out, and_27_out, and_28_out, and_29_out, and_30_out);
  or or_7 (C, and_31_out, and_32_out, and_33_out, and_34_out, and_35_out);
endmodule

module Comparator_3bit_maxorminoreql (
  input  A2,
  input  B2,
  input  A1,
  input  B1,
  input  A0,
  input  B0,
  output Gt,
  output Eq,
  output Lt
);

  wire and_1_out, and_2_out, and_3_out, and_4_out, C0_a_eq_b, C0_a_gt_b, C0_a_lt_b, C1_a_eq_b, C1_a_gt_b,
       C1_a_lt_b, C2_a_eq_b, C2_a_gt_b, C2_a_lt_b;

  Comparator_1bit_maxorminoreql C2 (.A(A2), .B(B2), .A_lt_B(C2_a_lt_b), .A_gt_B(C2_a_gt_b), .A_eq_B(C2_a_eq_b));
  Comparator_1bit_maxorminoreql C1 (.A(A1), .B(B1), .A_lt_B(C1_a_lt_b), .A_gt_B(C1_a_gt_b), .A_eq_B(C1_a_eq_b));
  Comparator_1bit_maxorminoreql C0 (.A(A0), .B(B0), .A_lt_B(C0_a_lt_b), .A_gt_B(C0_a_gt_b), .A_eq_B(C0_a_eq_b));
  and and_1 (and_1_out, C2_a_eq_b, C1_a_gt_b);
  and and_2 (and_2_out, C2_a_eq_b, C1_a_eq_b, C0_a_gt_b);
  and and_3 (and_3_out, C2_a_eq_b, C1_a_lt_b);
  and and_4 (and_4_out, C2_a_eq_b, C1_a_eq_b, C0_a_lt_b);
  or or_1 (Gt, C2_a_gt_b, and_1_out, and_2_out);
  and and_5 (Eq, C2_a_eq_b, C1_a_eq_b, C0_a_eq_b);
  or or_2 (Lt, C2_a_lt_b, and_3_out, and_4_out);
endmodule

module Comparator_1bit_maxorminoreql (
  input  A,
  input  B,
  output A_gt_B,
  output A_eq_B,
  output A_lt_B
);

  wire and_2_out, and_3_out, not_1_out, not_2_out;

  not not_1 (not_1_out, A);
  not not_2 (not_2_out, B);
  and and_1 (A_gt_B, A, not_2_out);
  and and_2 (and_2_out, not_1_out, not_2_out);
  and and_3 (and_3_out, A, B);
  and and_4 (A_lt_B, not_1_out, B);
  or or_1 (A_eq_B, and_2_out, and_3_out);
endmodule

module Full_Adder_4bit (
  input  A0,
  input  B0,
  input  Cin,
  input  A1,
  input  B1,
  input  A2,
  input  B2,
  input  A3,
  input  B3,
  output S0,
  output S1,
  output S2,
  output S3,
  output Count
);

  wire full_adder_1bit_1_count, full_adder_1bit_2_count, full_adder_1bit_3_count;

  Full_Adder_1bit full_adder_1bit_1 (.A(A0), .B(B0), .Cin(Cin), .Sum(S0), .Count(full_adder_1bit_1_count));
  Full_Adder_1bit full_adder_1bit_2 (
    .A(A1), .B(B1), .Cin(full_adder_1bit_1_count), .Sum(S1), .Count(full_adder_1bit_2_count));
  Full_Adder_1bit full_adder_1bit_3 (
    .A(A2), .B(B2), .Cin(full_adder_1bit_2_count), .Sum(S2), .Count(full_adder_1bit_3_count));
  Full_Adder_1bit full_adder_1bit_4 (.A(A3), .B(B3), .Cin(full_adder_1bit_3_count), .Sum(S3), .Count(Count));
endmodule

module Full_Adder_8bit (
  input  [7:0] A,
  input  [7:0] B,
  output [7:0] Sum
);

  wire full_adder_4bit_1_count;

  Full_Adder_4bit full_adder_4bit_1 (
    .A0(A[0]), .B0(B[0]), .A1(A[1]), .B1(B[1]), .A2(A[2]), .B2(B[2]), .A3(A[3]), .B3(B[3]), .S0(Sum[0]),
    .S1(Sum[1]), .S2(Sum[2]), .S3(Sum[3]), .Count(full_adder_4bit_1_count));  // open: Cin
  Full_Adder_4bit full_adder_4bit_2 (
    .A0(A[4]), .B0(B[4]), .Cin(full_adder_4bit_1_count), .A1(A[5]), .B1(B[5]), .A2(A[6]), .B2(B[6]),
    .A3(A[7]), .B3(B[7]), .S0(Sum[4]), .S1(Sum[5]), .S2(Sum[6]), .S3(Sum[7]));  // open: Count
endmodule

module Full_Adder_6bit (
  input  Cin,
  input  [5:0] A,
  input  [5:0] B,
  output [5:0] Sum,
  output Count
);

  wire full_adder_1bit_1_count, full_adder_4bit_1_count;

  Full_Adder_4bit full_adder_4bit_1 (
    .A0(A[0]), .B0(B[0]), .Cin(Cin), .A1(A[1]), .B1(B[1]), .A2(A[2]), .B2(B[2]), .A3(A[3]), .B3(B[3]),
    .S0(Sum[0]), .S1(Sum[1]), .S2(Sum[2]), .S3(Sum[3]), .Count(full_adder_4bit_1_count));
  Full_Adder_1bit full_adder_1bit_1 (
    .A(A[4]), .B(B[4]), .Cin(full_adder_4bit_1_count), .Sum(Sum[4]), .Count(full_adder_1bit_1_count));
  Full_Adder_1bit full_adder_1bit_2 (.A(A[5]), .B(B[5]), .Cin(full_adder_1bit_1_count), .Sum(Sum[5]), .Count(Count));
endmodule

module MUX_2to1_6bit (
  input  [5:0] A,
  input  [5:0] B,
  input  Sel,
  output [5:0] O
);

  MUX_2to1 mux_2to1_1 (.A(A[0]), .B(B[0]), .S(Sel), .Y(O[0]));
  MUX_2to1 mux_2to1_2 (.A(A[1]), .B(B[1]), .S(Sel), .Y(O[1]));
  MUX_2to1 mux_2to1_3 (.A(A[2]), .B(B[2]), .S(Sel), .Y(O[2]));
  MUX_2to1 mux_2to1_4 (.A(A[3]), .B(B[3]), .S(Sel), .Y(O[3]));
  MUX_2to1 mux_2to1_5 (.A(A[4]), .B(B[4]), .S(Sel), .Y(O[4]));
  MUX_2to1 mux_2to1_6 (.A(A[5]), .B(B[5]), .S(Sel), .Y(O[5]));
endmodule
