// Logisim project F3.6.3.circ as structural Verilog: 1 circuit, main circuit main
module main (
  input  [3:0] A,
  input  [3:0] B
);

  wire A_sm0, A_sm1, A_sm2, B_sm0, B_sm1, B_sm2, decoder_7_segment_display_1_a,
       decoder_7_segment_display_1_b, decoder_7_segment_display_1_c, decoder_7_segment_display_1_d,
       decoder_7_segment_display_1_e, decoder_7_segment_display_1_f, decoder_7_segment_display_1_g,
       decoder_7_segment_display_2_a, decoder_7_segment_display_2_b, decoder_7_segment_display_2_c,
       decoder_7_segment_display_2_d, decoder_7_segment_display_2_e, decoder_7_segment_display_2_f,
       decoder_7_segment_display_2_g, S0, S1, S2, S3, Y0, Y1, Y2;

  Sign_and_Magnitude_Adder_4bit sign_and_magnitude_adder_4bit_1 (
    .A({A[3], A_sm2, A_sm1, A_sm0}), .B({B[3], B_sm2, B_sm1, B_sm0}), .Y0(Y0), .Y1(Y1), .Y2(Y2), .Y3(S3));
  xor xor_1 (A_sm0, A[3], A[0]);
  xor xor_2 (A_sm1, A[3], A[1]);
  xor xor_3 (A_sm2, A[3], A[2]);
  _7_Segment_Display u_7_segment_display_1 (
    .g(S3), .f(1'b0), .a(1'b0), .b(1'b0), .e(1'b0), .d(1'b0), .c(1'b0), .dp(1'b0));
  _7_Segment_Display u_7_segment_display_2 (
    .g(S3), .f(1'b0), .a(1'b0), .b(1'b0), .e(1'b0), .d(1'b0), .c(1'b0), .dp(1'b0));
  xor xor_4 (B_sm0, B[3], B[0]);
  xor xor_5 (B_sm1, B[3], B[1]);
  xor xor_6 (B_sm2, B[3], B[2]);
  Decoder_7_Segment_Display decoder_7_segment_display_1 (
    .A2(Y2), .A0(Y0), .A1(Y1), .A(decoder_7_segment_display_1_a), .B(decoder_7_segment_display_1_b),
    .E(decoder_7_segment_display_1_e), .D(decoder_7_segment_display_1_d), .C(decoder_7_segment_display_1_c),
    .G(decoder_7_segment_display_1_g), .F(decoder_7_segment_display_1_f));  // open: A3
  Decoder_7_Segment_Display decoder_7_segment_display_2 (
    .A2(S2), .A0(S0), .A1(S1), .A(decoder_7_segment_display_2_a), .B(decoder_7_segment_display_2_b),
    .E(decoder_7_segment_display_2_e), .D(decoder_7_segment_display_2_d), .C(decoder_7_segment_display_2_c),
    .G(decoder_7_segment_display_2_g), .F(decoder_7_segment_display_2_f));  // open: A3
  _7_Segment_Display u_7_segment_display_3 (
    .g(decoder_7_segment_display_1_g), .f(decoder_7_segment_display_1_f), .a(decoder_7_segment_display_1_a),
    .b(decoder_7_segment_display_1_b), .e(decoder_7_segment_display_1_e), .d(decoder_7_segment_display_1_d),
    .c(decoder_7_segment_display_1_c));  // open: dp
  _7_Segment_Display u_7_segment_display_4 (
    .g(decoder_7_segment_display_2_g), .f(decoder_7_segment_display_2_f), .a(decoder_7_segment_display_2_a),
    .b(decoder_7_segment_display_2_b), .e(decoder_7_segment_display_2_e), .d(decoder_7_segment_display_2_d),
    .c(decoder_7_segment_display_2_c));  // open: dp
  xor xor_7 (S0, Y0, S3);
  xor xor_8 (S1, Y1, S3);
  xor xor_9 (S2, Y2, S3);

  // Other names for the same wires on the sheet: SA[3:0] = {A[3], A_sm2, A_sm1, A_sm0}; A_sm3 = A[3];
  //   SB[3:0] = {B[3], B_sm2, B_sm1, B_sm0}; B_sm3 = B[3]; Y3 = S3

  // Notes on the sheet:
  //   输入到原码加法器
  //   将输入的反码转换成原码
  //   原码结果
  //   反码结果
  //   将原码转换成反码
endmodule
