// Logisim project F3.6.4.circ as structural Verilog: 1 circuit, main circuit main
module main (
  input  [3:0] A,
  input  [3:0] B
);

  wire decoder_7_segment_display_1_a, decoder_7_segment_display_1_b, decoder_7_segment_display_1_c,
       decoder_7_segment_display_1_d, decoder_7_segment_display_1_e, decoder_7_segment_display_1_f,
       decoder_7_segment_display_1_g, full_adder_1bit_1_count, full_adder_1bit_1_sum,
       full_adder_1bit_2_count, full_adder_1bit_2_sum, full_adder_1bit_3_count, full_adder_1bit_3_sum,
       full_adder_1bit_4_count, full_adder_1bit_4_sum, full_adder_1bit_5_count, full_adder_1bit_6_count,
       full_adder_1bit_7_count, S0, S1, S2, S3;

  Full_Adder_1bit full_adder_1bit_1 (
    .A(A[0]), .B(B[0]), .Cin(1'b0), .Sum(full_adder_1bit_1_sum), .Count(full_adder_1bit_1_count));
  Full_Adder_1bit full_adder_1bit_2 (
    .A(A[1]), .B(B[1]), .Cin(full_adder_1bit_1_count), .Sum(full_adder_1bit_2_sum),
    .Count(full_adder_1bit_2_count));
  Full_Adder_1bit full_adder_1bit_3 (
    .A(A[2]), .B(B[2]), .Cin(full_adder_1bit_2_count), .Sum(full_adder_1bit_3_sum),
    .Count(full_adder_1bit_3_count));
  Full_Adder_1bit full_adder_1bit_4 (
    .A(A[3]), .B(B[3]), .Cin(full_adder_1bit_3_count), .Sum(full_adder_1bit_4_sum),
    .Count(full_adder_1bit_4_count));
  Full_Adder_1bit full_adder_1bit_5 (
    .A(full_adder_1bit_1_sum), .B(1'b0), .Cin(full_adder_1bit_4_count), .Sum(S0),
    .Count(full_adder_1bit_5_count));
  Full_Adder_1bit full_adder_1bit_6 (
    .A(full_adder_1bit_2_sum), .B(1'b0), .Cin(full_adder_1bit_5_count), .Sum(S1),
    .Count(full_adder_1bit_6_count));
  Full_Adder_1bit full_adder_1bit_7 (
    .A(full_adder_1bit_3_sum), .B(1'b0), .Cin(full_adder_1bit_6_count), .Sum(S2),
    .Count(full_adder_1bit_7_count));
  Full_Adder_1bit full_adder_1bit_8 (
    .A(full_adder_1bit_4_sum), .B(1'b0), .Cin(full_adder_1bit_7_count), .Sum(S3));  // open: Count
  _7_Segment_Display u_7_segment_display_1 (
    .g(S3), .f(1'b0), .a(1'b0), .b(1'b0), .e(1'b0), .d(1'b0), .c(1'b0), .dp(1'b0));
  Decoder_7_Segment_Display decoder_7_segment_display_1 (
    .A2(S2), .A0(S0), .A1(S1), .A(decoder_7_segment_display_1_a), .B(decoder_7_segment_display_1_b),
    .E(decoder_7_segment_display_1_e), .D(decoder_7_segment_display_1_d), .C(decoder_7_segment_display_1_c),
    .G(decoder_7_segment_display_1_g), .F(decoder_7_segment_display_1_f));  // open: A3
  _7_Segment_Display u_7_segment_display_2 (
    .g(decoder_7_segment_display_1_g), .f(decoder_7_segment_display_1_f), .a(decoder_7_segment_display_1_a),
    .b(decoder_7_segment_display_1_b), .e(decoder_7_segment_display_1_e), .d(decoder_7_segment_display_1_d),
    .c(decoder_7_segment_display_1_c));  // open: dp
endmodule
