// Logisim project F3.6_library .circ as structural Verilog: 1 circuit, main circuit Sign_and_Magnitude_Adder_4bit
module Sign_and_Magnitude_Adder_4bit (
  input  [3:0] A,
  input  [3:0] B,
  output Y0,
  output Y1,
  output Y2,
  output Y3
);

  wire A_ge_B, comparator_3bit_maxorminoreql_1_eq, comparator_3bit_maxorminoreql_1_gt, diff_A_B0, diff_A_B1,
       diff_A_B2, diff_B_A0, diff_B_A1, diff_B_A2, diff_result0, diff_result1, diff_result2, diff_sign,
       full_adder_1bit_1_count, full_adder_1bit_2_count, full_adder_1bit_4_count, full_adder_1bit_5_count,
       full_adder_1bit_7_count, full_adder_1bit_8_count, not_1_out, not_2_out, not_3_out, not_4_out,
       not_5_out, not_6_out, Sign_diff, sum_mag0, sum_mag1, sum_mag2;

  MUX_2to1 mux_2to1_1 (.A(diff_B_A0), .B(diff_A_B0), .S(A_ge_B), .Y(diff_result0));
  MUX_2to1 mux_2to1_2 (.A(diff_B_A1), .B(diff_A_B1), .S(A_ge_B), .Y(diff_result1));
  MUX_2to1 mux_2to1_3 (.A(diff_B_A2), .B(diff_A_B2), .S(A_ge_B), .Y(diff_result2));
  Comparator_3bit_maxorminoreql comparator_3bit_maxorminoreql_1 (
    .A2(A[2]), .B2(B[2]), .A1(A[1]), .B1(B[1]), .A0(A[0]), .B0(B[0]),
    .Gt(comparator_3bit_maxorminoreql_1_gt), .Eq(comparator_3bit_maxorminoreql_1_eq));  // open: Lt
  xor xor_1 (Sign_diff, A[3], B[3]);
  or or_1 (A_ge_B, comparator_3bit_maxorminoreql_1_gt, comparator_3bit_maxorminoreql_1_eq);
  not not_1 (not_1_out, B[0]);
  not not_2 (not_2_out, B[1]);
  not not_3 (not_3_out, B[2]);
  MUX_2to1 mux_2to1_4 (.A(sum_mag0), .B(diff_result0), .S(Sign_diff), .Y(Y0));
  MUX_2to1 mux_2to1_5 (.A(sum_mag1), .B(diff_result1), .S(Sign_diff), .Y(Y1));
  MUX_2to1 mux_2to1_6 (.A(sum_mag2), .B(diff_result2), .S(Sign_diff), .Y(Y2));
  Full_Adder_1bit full_adder_1bit_1 (
    .A(A[0]), .B(not_1_out), .Cin(1'b1), .Sum(diff_A_B0), .Count(full_adder_1bit_1_count));
  Full_Adder_1bit full_adder_1bit_2 (
    .A(A[1]), .B(not_2_out), .Cin(full_adder_1bit_1_count), .Sum(diff_A_B1), .Count(full_adder_1bit_2_count));
  Full_Adder_1bit full_adder_1bit_3 (
    .A(A[2]), .B(not_3_out), .Cin(full_adder_1bit_2_count), .Sum(diff_A_B2));  // open: Count
  Full_Adder_1bit full_adder_1bit_4 (.A(A[0]), .B(B[0]), .Cin(1'b0), .Sum(sum_mag0), .Count(full_adder_1bit_4_count));
  Full_Adder_1bit full_adder_1bit_5 (
    .A(A[1]), .B(B[1]), .Cin(full_adder_1bit_4_count), .Sum(sum_mag1), .Count(full_adder_1bit_5_count));
  Full_Adder_1bit full_adder_1bit_6 (.A(A[2]), .B(B[2]), .Cin(full_adder_1bit_5_count), .Sum(sum_mag2));  // open: Count
  not not_4 (not_4_out, A[0]);
  not not_5 (not_5_out, A[1]);
  not not_6 (not_6_out, A[2]);
  MUX_2to1 mux_2to1_7 (.A(B[3]), .B(A[3]), .S(A_ge_B), .Y(diff_sign));
  MUX_2to1 mux_2to1_8 (.A(A[3]), .B(diff_sign), .S(Sign_diff), .Y(Y3));
  Full_Adder_1bit full_adder_1bit_7 (
    .A(B[0]), .B(not_4_out), .Cin(1'b1), .Sum(diff_B_A0), .Count(full_adder_1bit_7_count));
  Full_Adder_1bit full_adder_1bit_8 (
    .A(B[1]), .B(not_5_out), .Cin(full_adder_1bit_7_count), .Sum(diff_B_A1), .Count(full_adder_1bit_8_count));
  Full_Adder_1bit full_adder_1bit_9 (
    .A(B[2]), .B(not_6_out), .Cin(full_adder_1bit_8_count), .Sum(diff_B_A2));  // open: Count

  // Other names for the same wires on the sheet: A_sign = A[3]; B_sign = B[3]; result_mag0 = Y0; result_mag1 = Y1;
  //   result_mag2 = Y2; result_sign = Y3
endmodule
