// Logisim project F3.7.12.circ as structural Verilog: 1 circuit, main circuit main
module main (
  input  in_1
);

  wire d_flip_flop_rst_4bit_1_p1, d_flip_flop_rst_4bit_1_p2, d_flip_flop_rst_4bit_1_p3,
       d_flip_flop_rst_4bit_1_p4, decoder_7_segment_display_1_a, decoder_7_segment_display_1_b,
       decoder_7_segment_display_1_c, decoder_7_segment_display_1_d, decoder_7_segment_display_1_e,
       decoder_7_segment_display_1_f, decoder_7_segment_display_1_g, dipswitch_1_p1, dipswitch_1_p2,
       dipswitch_1_p3, dipswitch_1_p4, dipswitch_1_p10;

  // DipSwitch #(.number(4)) dipswitch_1: pin names not known; wires that end beside it: dipswitch_1_p1, dipswitch_1_p2, dipswitch_1_p3, dipswitch_1_p4, in_1, dipswitch_1_p1, dipswitch_1_p2, dipswitch_1_p3, dipswitch_1_p4, dipswitch_1_p10
  Button button_1 (.out(dipswitch_1_p10));
  // D_Flip_Flop_RST_4bit d_flip_flop_rst_4bit_1: pin names not known; wires that end beside it: d_flip_flop_rst_4bit_1_p1, d_flip_flop_rst_4bit_1_p2, d_flip_flop_rst_4bit_1_p3, d_flip_flop_rst_4bit_1_p4
  Decoder_7_Segment_Display decoder_7_segment_display_1 (
    .A2(d_flip_flop_rst_4bit_1_p3), .A3(d_flip_flop_rst_4bit_1_p4), .A0(d_flip_flop_rst_4bit_1_p1),
    .A1(d_flip_flop_rst_4bit_1_p2), .A(decoder_7_segment_display_1_a), .B(decoder_7_segment_display_1_b),
    .E(decoder_7_segment_display_1_e), .D(decoder_7_segment_display_1_d), .C(decoder_7_segment_display_1_c),
    .G(decoder_7_segment_display_1_g), .F(decoder_7_segment_display_1_f));
  _7_Segment_Display u_7_segment_display_1 (
    .g(decoder_7_segment_display_1_g), .f(decoder_7_segment_display_1_f), .a(decoder_7_segment_display_1_a),
    .b(decoder_7_segment_display_1_b), .e(decoder_7_segment_display_1_e), .d(decoder_7_segment_display_1_d),
    .c(decoder_7_segment_display_1_c));  // open: dp
endmodule
