// Logisim project F3.7.13.circ as structural Verilog: 1 circuit, main circuit main
module main (
  input  RST,
  input  CLK
);

  wire d_register_4bit_1_q0, d_register_4bit_1_q1, d_register_4bit_1_q2, d_register_4bit_1_q3,
       decoder_7_segment_display_1_a, decoder_7_segment_display_1_b, decoder_7_segment_display_1_c,
       decoder_7_segment_display_1_d, decoder_7_segment_display_1_e, decoder_7_segment_display_1_f,
       decoder_7_segment_display_1_g;
  wire [3:0] full_adder_4bit_1_s0;

  D_Register_4bit d_register_4bit_1 (
    .RST(RST), .D0(full_adder_4bit_1_s0[0]), .D1(full_adder_4bit_1_s0[1]), .D2(full_adder_4bit_1_s0[2]),
    .D3(full_adder_4bit_1_s0[3]), .CLK(CLK), .Q0(d_register_4bit_1_q0), .Q1(d_register_4bit_1_q1),
    .Q2(d_register_4bit_1_q2), .Q3(d_register_4bit_1_q3));
  Decoder_7_Segment_Display decoder_7_segment_display_1 (
    .A2(d_register_4bit_1_q2), .A3(d_register_4bit_1_q3), .A0(d_register_4bit_1_q0),
    .A1(d_register_4bit_1_q1), .A(decoder_7_segment_display_1_a), .B(decoder_7_segment_display_1_b),
    .E(decoder_7_segment_display_1_e), .D(decoder_7_segment_display_1_d), .C(decoder_7_segment_display_1_c),
    .G(decoder_7_segment_display_1_g), .F(decoder_7_segment_display_1_f));
  Full_Adder_4bit full_adder_4bit_1 (
    .A0(d_register_4bit_1_q0), .B0(1'b1), .Cin(1'b0), .A1(d_register_4bit_1_q1), .B1(1'b0),
    .A2(d_register_4bit_1_q2), .B2(1'b0), .A3(d_register_4bit_1_q3), .B3(1'b0), .S0(full_adder_4bit_1_s0[0]),
    .S1(full_adder_4bit_1_s0[1]), .S2(full_adder_4bit_1_s0[2]), .S3(full_adder_4bit_1_s0[3]));  // open: Count
  _7_Segment_Display u_7_segment_display_1 (
    .g(decoder_7_segment_display_1_g), .f(decoder_7_segment_display_1_f), .a(decoder_7_segment_display_1_a),
    .b(decoder_7_segment_display_1_b), .e(decoder_7_segment_display_1_e), .d(decoder_7_segment_display_1_d),
    .c(decoder_7_segment_display_1_c));  // open: dp
endmodule
