// Logisim project F3.7.14.circ as structural Verilog: 1 circuit, main circuit main
module main (
  input  in_1,
  input  in_2
);

  wire decoder_7_segment_display_1_a, decoder_7_segment_display_1_b, decoder_7_segment_display_1_c,
       decoder_7_segment_display_1_d, decoder_7_segment_display_1_e, decoder_7_segment_display_1_f,
       decoder_7_segment_display_1_g, decoder_7_segment_display_2_a, decoder_7_segment_display_2_b,
       decoder_7_segment_display_2_c, decoder_7_segment_display_2_d, decoder_7_segment_display_2_e,
       decoder_7_segment_display_2_f, decoder_7_segment_display_2_g;
  wire [7:0] d_register_8bit_1_q, d_register_8bit_2_q, full_adder_8bit_1_sum, full_adder_8bit_2_sum;

  D_Register_8bit d_register_8bit_1 (.D(full_adder_8bit_1_sum), .RST(in_1), .CLK(in_2), .Q(d_register_8bit_1_q));
  D_Register_8bit d_register_8bit_2 (.D(full_adder_8bit_2_sum), .RST(in_1), .CLK(in_2), .Q(d_register_8bit_2_q));
  Full_Adder_8bit full_adder_8bit_1 (.A(d_register_8bit_1_q), .B(d_register_8bit_2_q), .Sum(full_adder_8bit_1_sum));
  Full_Adder_8bit full_adder_8bit_2 (.A(d_register_8bit_2_q), .B(8'h1), .Sum(full_adder_8bit_2_sum));
  Decoder_7_Segment_Display decoder_7_segment_display_1 (
    .A2(d_register_8bit_1_q[2]), .A3(d_register_8bit_1_q[3]), .A0(d_register_8bit_1_q[0]),
    .A1(d_register_8bit_1_q[1]), .A(decoder_7_segment_display_1_a), .B(decoder_7_segment_display_1_b),
    .E(decoder_7_segment_display_1_e), .D(decoder_7_segment_display_1_d), .C(decoder_7_segment_display_1_c),
    .G(decoder_7_segment_display_1_g), .F(decoder_7_segment_display_1_f));
  Decoder_7_Segment_Display decoder_7_segment_display_2 (
    .A2(d_register_8bit_1_q[6]), .A3(d_register_8bit_1_q[7]), .A0(d_register_8bit_1_q[4]),
    .A1(d_register_8bit_1_q[5]), .A(decoder_7_segment_display_2_a), .B(decoder_7_segment_display_2_b),
    .E(decoder_7_segment_display_2_e), .D(decoder_7_segment_display_2_d), .C(decoder_7_segment_display_2_c),
    .G(decoder_7_segment_display_2_g), .F(decoder_7_segment_display_2_f));
  _7_Segment_Display u_7_segment_display_1 (
    .g(decoder_7_segment_display_1_g), .f(decoder_7_segment_display_1_f), .a(decoder_7_segment_display_1_a),
    .b(decoder_7_segment_display_1_b), .e(decoder_7_segment_display_1_e), .d(decoder_7_segment_display_1_d),
    .c(decoder_7_segment_display_1_c));  // open: dp
  _7_Segment_Display u_7_segment_display_2 (
    .g(decoder_7_segment_display_2_g), .f(decoder_7_segment_display_2_f), .a(decoder_7_segment_display_2_a),
    .b(decoder_7_segment_display_2_b), .e(decoder_7_segment_display_2_e), .d(decoder_7_segment_display_2_d),
    .c(decoder_7_segment_display_2_c));  // open: dp
endmodule
