// Logisim project F3.7.15.circ as structural Verilog: 1 circuit, main circuit main
module main (
);

  wire and_1_out, clock_1_out, M0_a, M0_b, M0_c, M0_d, M0_e, M0_f, M0_g, M1_a, M1_b, M1_c, M1_d, M1_e, M1_f,
       M1_g, n74161_1_pin1, n74161_1_pin3, n74161_1_pin9, n74161_2_pin9, n74161_3_pin9, n74161_4_pin9,
       not_1_out, S0_a, S0_b, S0_c, S0_d, S0_e, S0_f, S0_g, S1_a, S1_b, S1_c, S1_d, S1_e, S1_f, S1_g, U0_A0,
       U0_A1, U0_A2, U0_A3, U1_A0, U1_A1, U1_A2, U1_A3, U2_A0, U2_A1, U2_A2, U2_A3, U3_A0, U3_A1, U3_A2,
       U3_A3;

  Clock clock_1 (.out(clock_1_out));
  _74161 u_74161_1 (
    .pin1(n74161_1_pin1), .pin2(clock_1_out), .pin3(n74161_1_pin3), .pin4(n74161_1_pin3),
    .pin5(n74161_1_pin3), .pin6(n74161_1_pin3), .pin7(n74161_1_pin1), .pin14(U0_A0), .pin13(U0_A1),
    .pin12(U0_A2), .pin11(U0_A3), .pin10(n74161_1_pin1), .pin9(n74161_1_pin9));  // open: pin15
  nand nand_1 (n74161_1_pin9, U0_A3, U0_A0);
  Decoder_7_Segment_Display M1 (
    .A2(U3_A2), .A3(U3_A3), .A0(U3_A0), .A1(U3_A1), .A(M1_a), .B(M1_b), .E(M1_e), .D(M1_d), .C(M1_c),
    .G(M1_g), .F(M1_f));
  _7_Segment_Display u_7_segment_display_1 (
    .g(M1_g), .f(M1_f), .a(M1_a), .b(M1_b), .e(M1_e), .d(M1_d), .c(M1_c));  // open: dp
  and and_1 (and_1_out, U0_A3, U0_A0);
  _74161 u_74161_2 (
    .pin1(n74161_1_pin1), .pin2(clock_1_out), .pin3(n74161_1_pin3), .pin4(n74161_1_pin3),
    .pin5(n74161_1_pin3), .pin6(n74161_1_pin3), .pin7(n74161_1_pin1), .pin14(U1_A0), .pin13(U1_A1),
    .pin12(U1_A2), .pin11(U1_A3), .pin10(and_1_out), .pin9(n74161_2_pin9));  // open: pin15
  nand nand_2 (n74161_2_pin9, U1_A0, U1_A2);
  Decoder_7_Segment_Display M0 (
    .A2(U2_A2), .A3(U2_A3), .A0(U2_A0), .A1(U2_A1), .A(M0_a), .B(M0_b), .E(M0_e), .D(M0_d), .C(M0_c),
    .G(M0_g), .F(M0_f));
  _7_Segment_Display u_7_segment_display_2 (
    .g(M0_g), .f(M0_f), .a(M0_a), .b(M0_b), .e(M0_e), .d(M0_d), .c(M0_c));  // open: dp
  _74161 u_74161_3 (
    .pin1(n74161_1_pin1), .pin2(n74161_2_pin9), .pin3(n74161_1_pin3), .pin4(n74161_1_pin3),
    .pin5(n74161_1_pin3), .pin6(n74161_1_pin3), .pin7(n74161_1_pin1), .pin14(U2_A0), .pin13(U2_A1),
    .pin12(U2_A2), .pin11(U2_A3), .pin10(n74161_1_pin1), .pin9(n74161_3_pin9));  // open: pin15
  nand nand_3 (n74161_3_pin9, U2_A0, U2_A3);
  not not_1 (not_1_out, n74161_3_pin9);
  Decoder_7_Segment_Display S1 (
    .A2(U1_A2), .A3(U1_A3), .A0(U1_A0), .A1(U1_A1), .A(S1_a), .B(S1_b), .E(S1_e), .D(S1_d), .C(S1_c),
    .G(S1_g), .F(S1_f));
  _7_Segment_Display u_7_segment_display_3 (
    .g(S1_g), .f(S1_f), .a(S1_a), .b(S1_b), .e(S1_e), .d(S1_d), .c(S1_c));  // open: dp
  _74161 u_74161_4 (
    .pin1(n74161_1_pin1), .pin2(n74161_2_pin9), .pin3(n74161_1_pin3), .pin4(n74161_1_pin3),
    .pin5(n74161_1_pin3), .pin6(n74161_1_pin3), .pin7(n74161_1_pin1), .pin14(U3_A0), .pin13(U3_A1),
    .pin12(U3_A2), .pin11(U3_A3), .pin10(not_1_out), .pin9(n74161_4_pin9));  // open: pin15
  nand nand_4 (n74161_4_pin9, U3_A0, U3_A2);
  Decoder_7_Segment_Display S0 (
    .A2(U0_A2), .A3(U0_A3), .A0(U0_A0), .A1(U0_A1), .A(S0_a), .B(S0_b), .E(S0_e), .D(S0_d), .C(S0_c),
    .G(S0_g), .F(S0_f));
  _7_Segment_Display u_7_segment_display_4 (
    .g(S0_g), .f(S0_f), .a(S0_a), .b(S0_b), .e(S0_e), .d(S0_d), .c(S0_c));  // open: dp
  // also tied to GND on the sheet: n74161_1_pin3
  // also tied to VCC on the sheet: n74161_1_pin1
endmodule
