// Logisim project F3.7.2.circ as structural Verilog: 1 circuit, main circuit main
module main (
  input  R,
  input  S,
  output NQ,
  output Q
);

  nand nand_1 (NQ, R, Q);
  nand nand_2 (Q, NQ, S);
endmodule
