// Logisim project F3.7.4.circ as structural Verilog: 1 circuit, main circuit main
module main (
  input  D,
  input  WE,
  output Q,
  output NQ
);

  wire and_1_out, and_2_out, not_1_out;

  not not_1 (not_1_out, D);
  and and_1 (and_1_out, not_1_out, WE);
  and and_2 (and_2_out, WE, D);
  SR_Latch sr_latch_1 (.S(and_1_out), .R(and_2_out), .NQ(Q), .Q(NQ));
endmodule
