// Logisim project F3.7.7.circ as structural Verilog: 1 circuit, main circuit main
module main (
  input  in_1
);

  wire button_1_out, d_flip_flop_1_q;

  Button button_1 (.out(button_1_out));
  D_Flip_Flop d_flip_flop_1 (.CLK(button_1_out), .D(in_1), .Q(d_flip_flop_1_q));
  LED led_1 (.in(d_flip_flop_1_q));
endmodule
