// Logisim project F3.7_library.circ as structural Verilog: 12 circuits, main circuit SR_Latch
module SR_Latch (
  input  S,
  input  R,
  output NQ,
  output Q
);

  nor nor_1 (NQ, S, Q);
  nor nor_2 (Q, NQ, R);
endmodule

module D_Latch (
  input  D,
  input  WE,
  output Q,
  output NQ
);

  wire and_1_out, and_2_out, not_1_out;

  not not_1 (not_1_out, D);
  and and_1 (and_1_out, not_1_out, WE);
  and and_2 (and_2_out, WE, D);
  SR_Latch sr_latch_1 (.S(and_1_out), .R(and_2_out), .NQ(Q), .Q(NQ));
endmodule

module D_Latch_RST (
  input  RST,
  input  D,
  input  WE,
  output Q,
  output NQ
);

  wire and_1_out, and_2_out, and_3_out, not_1_out, not_2_out, or_1_out;

  not not_1 (not_1_out, RST);
  not not_2 (not_2_out, D);
  and and_1 (and_1_out, not_2_out, WE);
  and and_2 (and_2_out, D, WE);
  or or_1 (or_1_out, RST, and_1_out);
  and and_3 (and_3_out, not_1_out, and_2_out);
  SR_Latch sr_latch_1 (.S(or_1_out), .R(and_3_out), .NQ(Q), .Q(NQ));
endmodule

module D_Latch_return (
  output out_1
);

  wire d_latch_rst_1_q, dipswitch_1_p1;

  // DipSwitch #(.number(1)) dipswitch_1: pin names not known; wires that end beside it: dipswitch_1_p1
  D_Latch_RST d_latch_rst_1 (.RST(dipswitch_1_p1), .D(out_1), .WE(1'b1), .Q(d_latch_rst_1_q));  // open: NQ
  not not_1 (out_1, d_latch_rst_1_q);
endmodule

module D_Flip_Flop (
  input  D,
  input  CLK,
  output Q
);

  wire d_latch_1_q, not_1_out;

  not not_1 (not_1_out, CLK);
  D_Latch d_latch_1 (.D(D), .WE(not_1_out), .Q(d_latch_1_q));  // open: NQ
  D_Latch d_latch_2 (.D(d_latch_1_q), .WE(CLK), .Q(Q));  // open: NQ
endmodule

module D_Flip_Flop_RST (
  input  RST,
  input  D,
  input  CLK,
  output Q
);

  wire d_latch_rst_1_q, not_1_out;

  not not_1 (not_1_out, CLK);
  D_Latch_RST d_latch_rst_1 (.RST(RST), .D(D), .WE(not_1_out), .Q(d_latch_rst_1_q));  // open: NQ
  D_Latch_RST d_latch_rst_2 (.RST(RST), .D(d_latch_rst_1_q), .WE(CLK), .Q(Q));  // open: NQ
endmodule

module D_Flip_Flop_return (
  input  RST,
  input  CLK,
  output out_3
);

  wire d_flip_flop_rst_1_q;

  D_Flip_Flop_RST d_flip_flop_rst_1 (.CLK(CLK), .RST(RST), .D(out_3), .Q(d_flip_flop_rst_1_q));
  not not_1 (out_3, d_flip_flop_rst_1_q);
endmodule

module D_Flip_Flop_N_Edge (
  input  D,
  input  CLK,
  output Q
);

  wire d_latch_1_q, not_1_out;

  D_Latch d_latch_1 (.D(D), .WE(CLK), .Q(d_latch_1_q));  // open: NQ
  not not_1 (not_1_out, CLK);
  D_Latch d_latch_2 (.D(d_latch_1_q), .WE(not_1_out), .Q(Q));  // open: NQ
endmodule

module D_Register_4bit (
  input  RST,
  input  D0,
  input  D1,
  input  D2,
  input  D3,
  input  CLK,
  output Q0,
  output Q1,
  output Q2,
  output Q3
);

  D_Flip_Flop_RST d_flip_flop_rst_1 (.CLK(CLK), .RST(RST), .D(D0), .Q(Q0));
  D_Flip_Flop_RST d_flip_flop_rst_2 (.CLK(CLK), .RST(RST), .D(D1), .Q(Q1));
  D_Flip_Flop_RST d_flip_flop_rst_3 (.CLK(CLK), .RST(RST), .D(D2), .Q(Q2));
  D_Flip_Flop_RST d_flip_flop_rst_4 (.CLK(CLK), .RST(RST), .D(D3), .Q(Q3));
endmodule

module Counter_4_Bit (
  input  RST,
  input  CLK,
  output Q0,
  output Q1,
  output Q2,
  output Q3
);

  wire [3:0] full_adder_4bit_1_s0;

  D_Register_4bit d_register_4bit_1 (
    .RST(RST), .D0(full_adder_4bit_1_s0[0]), .D1(full_adder_4bit_1_s0[1]), .D2(full_adder_4bit_1_s0[2]),
    .D3(full_adder_4bit_1_s0[3]), .CLK(CLK), .Q0(Q0), .Q1(Q1), .Q2(Q2), .Q3(Q3));
  Full_Adder_4bit full_adder_4bit_1 (
    .A0(Q0), .B0(1'b1), .Cin(1'b0), .A1(Q1), .B1(1'b0), .A2(Q2), .B2(1'b0), .A3(Q3), .B3(1'b0),
    .S0(full_adder_4bit_1_s0[0]), .S1(full_adder_4bit_1_s0[1]), .S2(full_adder_4bit_1_s0[2]),
    .S3(full_adder_4bit_1_s0[3]));  // open: Count
endmodule

module D_Register_8bit (
  input  RST,
  input  [7:0] D,
  input  CLK,
  output [7:0] Q
);

  D_Register_4bit d_register_4bit_1 (
    .RST(RST), .D0(D[0]), .D1(D[1]), .D2(D[2]), .D3(D[3]), .CLK(CLK), .Q0(Q[0]), .Q1(Q[1]), .Q2(Q[2]),
    .Q3(Q[3]));
  D_Register_4bit d_register_4bit_2 (
    .RST(RST), .D0(D[4]), .D1(D[5]), .D2(D[6]), .D3(D[7]), .CLK(CLK), .Q0(Q[4]), .Q1(Q[5]), .Q2(Q[6]),
    .Q3(Q[7]));
endmodule

module D_Register_6bit (
  input  RST,
  input  [5:0] D,
  input  CLK,
  output [5:0] Q
);

  D_Register_4bit d_register_4bit_1 (
    .RST(RST), .D0(D[0]), .D1(D[1]), .D2(D[2]), .D3(D[3]), .CLK(CLK), .Q0(Q[0]), .Q1(Q[1]), .Q2(Q[2]),
    .Q3(Q[3]));
  D_Flip_Flop_RST d_flip_flop_rst_1 (.CLK(CLK), .RST(RST), .D(D[4]), .Q(Q[4]));
  D_Flip_Flop_RST d_flip_flop_rst_2 (.CLK(CLK), .RST(RST), .D(D[5]), .Q(Q[5]));
endmodule
