// Logisim project F5.1.1.circ as structural Verilog: 1 circuit, main circuit main
module main (
  input  CLK,
  output [7:0] out_2
);

  wire [3:0] adder_1_out, PC_q;

  Register #(.width(4)) PC (.D(adder_1_out), .Q(PC_q), .clk(CLK));  // open: en, clr
  Adder #(.width(4)) adder_1 (.a(PC_q), .b(4'b0001), .out(adder_1_out));  // open: cin, cout
  Multiplexer #(.select(4), .width(8)) multiplexer_1 (
    .in0(8'h90), .in1(8'haa), .in2(8'h8f), .in3(8'h16), .in4(8'h2b), .in5(8'hce), .in6(8'hd8),
    .in7({8{1'b0}}), .in8({8{1'b0}}), .in9({8{1'b0}}), .in10({8{1'b0}}), .in11({8{1'b0}}), .in12({8{1'b0}}),
    .in13({8{1'b0}}), .in14({8{1'b0}}), .in15({8{1'b0}}), .out(out_2), .sel(PC_q));
endmodule
