// Logisim project F5.1.circ as structural Verilog: 1 circuit, main circuit main
module main (
);

  wire and_1_out, and_2_out, and_3_out, and_4_out, clock_1_out, comparator_1_gt, comparator_1_lt,
       decoder_1_out0, decoder_1_out1, decoder_1_out2, decoder_1_out3, decoder_2_out0, decoder_2_out1,
       decoder_2_out2, decoder_2_out3, decoder_7_segment_display_1_a, decoder_7_segment_display_1_b,
       decoder_7_segment_display_1_c, decoder_7_segment_display_1_d, decoder_7_segment_display_1_e,
       decoder_7_segment_display_1_f, decoder_7_segment_display_1_g, decoder_7_segment_display_2_a,
       decoder_7_segment_display_2_b, decoder_7_segment_display_2_c, decoder_7_segment_display_2_d,
       decoder_7_segment_display_2_e, decoder_7_segment_display_2_f, decoder_7_segment_display_2_g, jump,
       or_2_out, wen;
  wire [1:0] raddr1, raddr2, waddr;
  wire [3:0] adder_1_out, multiplexer_1_out, PC_q;
  wire [7:0] adder_2_out, bit_extender_1_out, r0_q, r1_q, r2_q, r3_q, rdata1, rdata2, register_1_q, wdata;
  wire [7:6] multiplexer_2_out;

  Clock clock_1 (.out(clock_1_out));
  Multiplexer #(.width(4)) multiplexer_1 (
    .in0(adder_1_out), .in1({waddr, raddr1}), .out(multiplexer_1_out), .sel(jump));
  Register #(.width(4)) PC (.D(multiplexer_1_out), .Q(PC_q), .clk(clock_1_out));  // open: en, clr
  Adder #(.width(4)) adder_1 (.a(PC_q), .b(4'b0001), .out(adder_1_out));  // open: cin, cout
  Decoder #(.select(2)) decoder_1 (
    .out0(decoder_1_out0), .out1(decoder_1_out1), .out2(decoder_1_out2), .out3(decoder_1_out3), .sel(waddr),
    .en(wen));
  Multiplexer #(.select(4), .width(8)) multiplexer_2 (
    .in0(8'h8b), .in1(8'h91), .in2(8'ha0), .in3(8'hb2), .in4(8'h29), .in5(8'h17), .in6(8'hd1), .in7(8'h42),
    .in8(8'hdf), .out({multiplexer_2_out, waddr, raddr1, raddr2}), .sel(PC_q));  // open: in9, in10, in11, in12, in13, in14, in15
  and and_1 (and_1_out, decoder_1_out0, wen);
  and and_2 (and_2_out, decoder_1_out1, wen);
  and and_3 (and_3_out, decoder_1_out2, wen);
  and and_4 (and_4_out, decoder_1_out3, wen);
  Register r0 (.D(wdata), .en(and_1_out), .Q(r0_q), .clk(clock_1_out));  // open: clr
  Register r1 (.D(wdata), .en(and_2_out), .Q(r1_q), .clk(clock_1_out));  // open: clr
  Register r2 (.D(wdata), .en(and_3_out), .Q(r2_q), .clk(clock_1_out));  // open: clr
  Register r3 (.D(wdata), .en(and_4_out), .Q(r3_q), .clk(clock_1_out));  // open: clr
  Decoder #(.select(2)) decoder_2 (
    .out0(decoder_2_out0), .out1(decoder_2_out1), .out2(decoder_2_out2), .out3(decoder_2_out3),
    .sel(multiplexer_2_out));  // open: en
  Multiplexer #(.select(2), .width(8)) multiplexer_3 (
    .in0(r0_q), .in1(r1_q), .in2(r2_q), .in3(r3_q), .out(rdata1), .sel(raddr1));
  Multiplexer #(.select(2), .width(8)) multiplexer_4 (
    .in0(r0_q), .in1(r1_q), .in2(r2_q), .in3(r3_q), .out(rdata2), .sel(raddr2));
  assign bit_extender_1_out = {{4{1'b0}}, {raddr1, raddr2}};  // Bit_Extender bit_extender_1
  or or_1 (wen, decoder_2_out0, decoder_2_out2);
  Register register_1 (.D(rdata2), .en(decoder_2_out1), .Q(register_1_q), .clk(clock_1_out));  // open: clr
  Comparator comparator_1 (.a(rdata1), .b(rdata2), .gt(comparator_1_gt), .lt(comparator_1_lt));  // open: eq
  Adder adder_2 (.a(rdata1), .b(rdata2), .out(adder_2_out));  // open: cin, cout
  Multiplexer #(.width(8)) multiplexer_5 (
    .in0(adder_2_out), .in1(bit_extender_1_out), .out(wdata), .sel(decoder_2_out2));
  or or_2 (or_2_out, comparator_1_gt, comparator_1_lt);
  and and_5 (jump, decoder_2_out3, or_2_out);
  Decoder_7_Segment_Display decoder_7_segment_display_1 (
    .A2(register_1_q[6]), .A3(register_1_q[7]), .A0(register_1_q[4]), .A1(register_1_q[5]),
    .A(decoder_7_segment_display_1_a), .B(decoder_7_segment_display_1_b), .E(decoder_7_segment_display_1_e),
    .D(decoder_7_segment_display_1_d), .C(decoder_7_segment_display_1_c), .G(decoder_7_segment_display_1_g),
    .F(decoder_7_segment_display_1_f));
  _7_Segment_Display u_7_segment_display_1 (
    .g(decoder_7_segment_display_1_g), .f(decoder_7_segment_display_1_f), .a(decoder_7_segment_display_1_a),
    .b(decoder_7_segment_display_1_b), .e(decoder_7_segment_display_1_e), .d(decoder_7_segment_display_1_d),
    .c(decoder_7_segment_display_1_c));  // open: dp
  Decoder_7_Segment_Display decoder_7_segment_display_2 (
    .A2(register_1_q[2]), .A3(register_1_q[3]), .A0(register_1_q[0]), .A1(register_1_q[1]),
    .A(decoder_7_segment_display_2_a), .B(decoder_7_segment_display_2_b), .E(decoder_7_segment_display_2_e),
    .D(decoder_7_segment_display_2_d), .C(decoder_7_segment_display_2_c), .G(decoder_7_segment_display_2_g),
    .F(decoder_7_segment_display_2_f));
  _7_Segment_Display u_7_segment_display_2 (
    .g(decoder_7_segment_display_2_g), .f(decoder_7_segment_display_2_f), .a(decoder_7_segment_display_2_a),
    .b(decoder_7_segment_display_2_b), .e(decoder_7_segment_display_2_e), .d(decoder_7_segment_display_2_d),
    .c(decoder_7_segment_display_2_c));  // open: dp
endmodule
