// Logisim project F5_library.circ as structural Verilog: 2 circuits, main circuit GPR
module GPR (
  input  CLK,
  input  [7:0] wdata,
  input  wen,
  input  [1:0] waddr,
  input  [1:0] raddr1,
  input  [1:0] raddr2,
  output [7:0] rdata1,
  output [7:0] rdata2
);

  wire and_1_out, and_2_out, and_3_out, and_4_out, decoder_1_out0, decoder_1_out1, decoder_1_out2,
       decoder_1_out3;
  wire [7:0] r0_q, r1_q, r2_q, r3_q;

  Decoder #(.select(2)) decoder_1 (
    .out0(decoder_1_out0), .out1(decoder_1_out1), .out2(decoder_1_out2), .out3(decoder_1_out3), .sel(waddr),
    .en(wen));
  and and_1 (and_1_out, decoder_1_out0, wen);
  and and_2 (and_2_out, decoder_1_out1, wen);
  and and_3 (and_3_out, decoder_1_out2, wen);
  and and_4 (and_4_out, decoder_1_out3, wen);
  Register r0 (.D(wdata), .en(and_1_out), .Q(r0_q), .clk(CLK));  // open: clr
  Register r1 (.D(wdata), .en(and_2_out), .Q(r1_q), .clk(CLK));  // open: clr
  Register r2 (.D(wdata), .en(and_3_out), .Q(r2_q), .clk(CLK));  // open: clr
  Register r3 (.D(wdata), .en(and_4_out), .Q(r3_q), .clk(CLK));  // open: clr
  Multiplexer #(.select(2), .width(8)) multiplexer_1 (
    .in0(r0_q), .in1(r1_q), .in2(r2_q), .in3(r3_q), .out(rdata1), .sel(raddr1));
  Multiplexer #(.select(2), .width(8)) multiplexer_2 (
    .in0(r0_q), .in1(r1_q), .in2(r2_q), .in3(r3_q), .out(rdata2), .sel(raddr2));
endmodule

module PC_ROM (
  input  CLK,
  output [7:0] out_2
);

  wire [3:0] adder_1_out, PC_q;

  Register #(.width(4)) PC (.D(adder_1_out), .Q(PC_q), .clk(CLK));  // open: en, clr
  Adder #(.width(4)) adder_1 (.a(PC_q), .b(4'b0001), .out(adder_1_out));  // open: cin, cout
  Multiplexer #(.select(4), .width(8)) multiplexer_1 (
    .in0(8'h90), .in1(8'haa), .in2(8'hbf), .in3(8'h16), .in4(8'h2b), .in5(8'hce), .in6(8'hd8), .out(out_2),
    .sel(PC_q));  // open: in7, in8, in9, in10, in11, in12, in13, in14, in15
endmodule
