// Logisim project miniriscv.circ as structural Verilog: 1 circuit, main circuit main
module main (
);

  wire clock_1_out, comparator_1_eq, comparator_2_eq, comparator_3_eq, decoder_1_out1, decoder_1_out2,
       decoder_1_out3, decoder_1_out4, decoder_1_out5, decoder_1_out6, decoder_1_out7, decoder_1_out8,
       decoder_1_out9, decoder_1_out10, decoder_1_out11, decoder_1_out12, decoder_1_out13, decoder_1_out14,
       decoder_1_out15, is_addi, is_jalr, regwrite;
  wire [2:0] funct3;
  wire [3:0] raddr1, raddr2, waddr;
  wire [6:0] opcode;
  wire [31:0] ALU_out, imm32, multiplexer_1_out, PC_next, PC_q, rdata1, rdata2, register_1_q, register_2_q,
       register_3_q, register_4_q, register_5_q, register_6_q, register_7_q, register_8_q, register_9_q,
       register_10_q, register_11_q, register_12_q, register_13_q, register_14_q, register_15_q, wdata;
  wire [31:11] rom_1_data;

  Clock clock_1 (.out(clock_1_out));
  Multiplexer #(.width(32)) multiplexer_1 (
    .in0(PC_next), .in1({ALU_out[31:1], 1'b0}), .out(multiplexer_1_out), .sel(is_jalr));
  Decoder #(.select(4)) decoder_1 (
    .out1(decoder_1_out1), .out2(decoder_1_out2), .out3(decoder_1_out3), .out4(decoder_1_out4),
    .out5(decoder_1_out5), .out6(decoder_1_out6), .out7(decoder_1_out7), .out8(decoder_1_out8),
    .out9(decoder_1_out9), .out10(decoder_1_out10), .out11(decoder_1_out11), .out12(decoder_1_out12),
    .out13(decoder_1_out13), .out14(decoder_1_out14), .out15(decoder_1_out15), .sel(waddr), .en(regwrite));  // open: out0
  Register #(.width(32)) PC (.D(multiplexer_1_out), .Q(PC_q), .clk(clock_1_out));  // open: en, clr
  Adder #(.width(32)) adder_1 (.a(PC_q), .b(32'h4), .out(PC_next));  // open: cin, cout
  Comparator #(.width(7)) comparator_1 (.a(opcode), .b(7'b0010011), .eq(comparator_1_eq));  // open: gt, lt
  Comparator #(.width(7)) comparator_2 (.a(opcode), .b(7'b1100111), .eq(comparator_2_eq));  // open: gt, lt
  Comparator #(.width(3)) comparator_3 (.a(funct3), .b(3'b000), .eq(comparator_3_eq));  // open: gt, lt
  Register #(.width(32)) register_1 (.D(wdata), .en(decoder_1_out8), .clk(clock_1_out), .Q(register_1_q));  // open: clr
  ROM #(.dataWidth(32)) rom_1 (
    .addr(PC_q[9:2]), .data({rom_1_data[31:19], raddr1, funct3, rom_1_data[11], waddr, opcode}));
  Register #(.width(32)) register_2 (.D(wdata), .en(decoder_1_out1), .clk(clock_1_out), .Q(register_2_q));  // open: clr
  Register #(.width(32)) register_3 (.D(wdata), .en(decoder_1_out9), .clk(clock_1_out), .Q(register_3_q));  // open: clr
  and and_1 (is_addi, comparator_1_eq, comparator_3_eq);
  and and_2 (is_jalr, comparator_2_eq, comparator_3_eq);
  Register #(.width(32)) register_4 (.D(wdata), .en(decoder_1_out2), .clk(clock_1_out), .Q(register_4_q));  // open: clr
  Register #(.width(32)) register_5 (
    .D(wdata), .en(decoder_1_out10), .clk(clock_1_out), .Q(register_5_q));  // open: clr
  Register #(.width(32)) register_6 (.D(wdata), .en(decoder_1_out3), .clk(clock_1_out), .Q(register_6_q));  // open: clr
  Register #(.width(32)) register_7 (
    .D(wdata), .en(decoder_1_out11), .clk(clock_1_out), .Q(register_7_q));  // open: clr
  Register #(.width(32)) register_8 (.D(wdata), .en(decoder_1_out4), .clk(clock_1_out), .Q(register_8_q));  // open: clr
  Register #(.width(32)) register_9 (
    .D(wdata), .en(decoder_1_out12), .clk(clock_1_out), .Q(register_9_q));  // open: clr
  or or_1 (regwrite, is_addi, is_jalr);
  Register #(.width(32)) register_10 (
    .D(wdata), .en(decoder_1_out5), .clk(clock_1_out), .Q(register_10_q));  // open: clr
  Register #(.width(32)) register_11 (
    .D(wdata), .en(decoder_1_out13), .clk(clock_1_out), .Q(register_11_q));  // open: clr
  Register #(.width(32)) register_12 (
    .D(wdata), .en(decoder_1_out6), .clk(clock_1_out), .Q(register_12_q));  // open: clr
  Register #(.width(32)) register_13 (
    .D(wdata), .en(decoder_1_out14), .clk(clock_1_out), .Q(register_13_q));  // open: clr
  assign imm32 = {{20{rom_1_data[31]}}, rom_1_data[31:20]};  // Bit_Extender bit_extender_1
  Register #(.width(32)) register_14 (
    .D(wdata), .en(decoder_1_out7), .clk(clock_1_out), .Q(register_14_q));  // open: clr
  Register #(.width(32)) register_15 (
    .D(wdata), .en(decoder_1_out15), .clk(clock_1_out), .Q(register_15_q));  // open: clr
  Multiplexer #(.width(32)) multiplexer_2 (.in0(ALU_out), .in1(PC_next), .out(wdata), .sel(is_jalr));
  Adder #(.width(32)) adder_2 (.a(rdata1), .b(imm32), .out(ALU_out));  // open: cin, cout
  Multiplexer #(.select(4), .width(32)) multiplexer_3 (
    .in0({32{1'b0}}), .in1(register_2_q), .in2(register_4_q), .in3(register_6_q), .in4(register_8_q),
    .in5(register_10_q), .in6(register_12_q), .in7(register_14_q), .in8(register_1_q), .in9(register_3_q),
    .in10(register_5_q), .in11(register_7_q), .in12(register_9_q), .in13(register_11_q),
    .in14(register_13_q), .in15(register_15_q), .out(rdata1), .sel(raddr1));
  Multiplexer #(.select(4), .width(32)) multiplexer_4 (
    .in0({32{1'b0}}), .in1(register_2_q), .in2(register_4_q), .in3(register_6_q), .in4(register_8_q),
    .in5(register_10_q), .in6(register_12_q), .in7(register_14_q), .in8(register_1_q), .in9(register_3_q),
    .in10(register_5_q), .in11(register_7_q), .in12(register_9_q), .in13(register_11_q),
    .in14(register_13_q), .in15(register_15_q), .out(rdata2), .sel(raddr2));

  // Other names for the same wires on the sheet: PC_target[31:1] = ALU_out[31:1]

  // Notes on the sheet:
  //   contents of rom_1 (hex, n*v repeats v):
  //   1400513 10000e7 c000e7 c00067 a50513 8067
  //   rs
  //   rs1
  //   ALU
  //   jalr低位清0电路
endmodule
