// Logisim project minirv.circ as structural Verilog: 1 circuit, main circuit main
module main (
);

  wire clock_1_out, clock_2_out, clock_3_out, clock_4_out, comparator_1_lt, comparator_2_lt, comparator_3_eq,
       comparator_4_eq, comparator_5_eq, comparator_6_eq, comparator_7_eq, comparator_8_eq, comparator_9_eq,
       comparator_11_eq, comparator_12_eq, comparator_13_eq, comparator_14_eq, comparator_15_eq,
       comparator_16_eq, comparator_17_eq, comparator_18_eq, decoder_1_out0, decoder_1_out1, decoder_1_out2,
       decoder_1_out3, decoder_1_out4, decoder_1_out5, decoder_1_out6, decoder_1_out7, decoder_1_out8,
       decoder_1_out9, decoder_1_out10, decoder_1_out11, decoder_1_out12, decoder_1_out13, decoder_1_out14,
       decoder_1_out15, decoder_2_out0, decoder_2_out1, decoder_2_out2, decoder_2_out3, is_add, is_addi,
       is_jalr, is_lbu, is_lui, is_lw, is_ram, is_RAM_IO, is_sb, is_sw, is_vga, not_1_out, or_2_out, RAM_BE0,
       RAM_BE1, RAM_BE2, RAM_BE3, RAM_WE, regwrite, vga_write;
  wire [1:0] sb_byte_selector;
  wire [2:0] funct3;
  wire [3:0] rs1_addr, rs2_addr, waddr;
  wire [4:0] bit_extender_18_out, I_Type_imm, lbu_byte_selector, multiplier_1_out, multiplier_2_out;
  wire [6:0] funct7, opcode;
  wire [19:7] operation;
  wire [23:0] bit_extender_1_out, bit_extender_3_out, vga_color;
  wire [31:0] adder_1_out, adder_2_out, adder_3_out, adder_4_out, adder_5_out, adder_6_out, adder_7_out,
       adder_8_out, and_11_out, and_12_out, and_13_out, bit_extender_4_out, bit_extender_5_out,
       bit_extender_6_out, bit_extender_15_out, bit_extender_16_out, bit_extender_17_out, mem_addr, mem_data,
       new_PC_data, PC_data, RAM_data, rs1_data, rs2_data, shifter_1_out, shifter_2_out, shifter_3_out,
       shifter_4_out, shifter_5_out, shifter_6_out, shifter_7_out, write_data, x1_ra_q, x2_sp_q, x3_gp_q,
       x4_tp_q, x5_t0_q, x6_t1_q, x7_t2_q, x8_s0_fp_q, x9_s1_q, x10_a0_q, x11_a1_q, x12_a2_q, x13_a3_q,
       x14_a4_q, x15_a5_q;

  Clock clock_1 (.out(clock_1_out));
  Clock clock_2 (.out(clock_2_out));
  Decoder #(.select(4)) decoder_1 (
    .out0(decoder_1_out0), .out1(decoder_1_out1), .out2(decoder_1_out2), .out3(decoder_1_out3),
    .out4(decoder_1_out4), .out5(decoder_1_out5), .out6(decoder_1_out6), .out7(decoder_1_out7),
    .out8(decoder_1_out8), .out9(decoder_1_out9), .out10(decoder_1_out10), .out11(decoder_1_out11),
    .out12(decoder_1_out12), .out13(decoder_1_out13), .out14(decoder_1_out14), .out15(decoder_1_out15),
    .sel(waddr), .en(regwrite));
  Counter #(.max('hffffffff), .width(32)) PC_counter (
    .load(is_jalr), .D(new_PC_data), .Q(PC_data), .up(1'b1), .clk(clock_1_out));  // open: count, carry, clr
  ROM #(.addrWidth(24), .dataWidth(32)) rom_1 (
    .addr(bit_extender_1_out), .data({funct7, I_Type_imm, operation[19:15], funct3, operation[11:7], opcode}));
  Bit_Extender #(.in_width(32), .out_width(24), .\type ("zero")) bit_extender_1 (
    .in(PC_data), .out(bit_extender_1_out));
  // NoConnect on decoder_1_out0
  or or_1 (is_RAM_IO, is_lw, is_lbu, is_sw, is_sb);
  or or_2 (or_2_out, is_sw, is_sb);
  and and_1 (RAM_WE, or_2_out, is_ram);
  and and_2 (vga_write, is_vga, is_sw);
  // NoConnect on mem_addr[1:0]
  // NoConnect on mem_addr[31:18]
  Bit_Extender #(.in_width(32), .out_width(24), .\type ("zero")) bit_extender_2 (.in(mem_data), .out(vga_color));
  Shifter #(.width(32)) shifter_1 (.in(PC_data), .\dist (5'b00010), .out(shifter_1_out));
  Register #(.width(32)) x0_zero (.D(write_data), .en(1'b0), .clk(clock_2_out));  // open: Q, clr
  Register #(.width(32)) x8_s0_fp (
    .D(write_data), .en(decoder_1_out8), .clk(clock_2_out), .Q(x8_s0_fp_q));  // open: clr
  or or_3 (regwrite, is_addi, is_jalr, is_add, is_lui, is_lw, is_lbu);
  // Probe on shifter_1_out
  Register #(.width(32)) x1_ra (.D(write_data), .en(decoder_1_out1), .clk(clock_2_out), .Q(x1_ra_q));  // open: clr
  Register #(.width(32)) x9_s1 (.D(write_data), .en(decoder_1_out9), .clk(clock_2_out), .Q(x9_s1_q));  // open: clr
  Register #(.width(32)) x2_sp (.D(write_data), .en(decoder_1_out2), .clk(clock_2_out), .Q(x2_sp_q));  // open: clr
  Register #(.width(32)) x10_a0 (.D(write_data), .en(decoder_1_out10), .clk(clock_2_out), .Q(x10_a0_q));  // open: clr
  Register #(.width(32)) x3_gp (.D(write_data), .en(decoder_1_out3), .clk(clock_2_out), .Q(x3_gp_q));  // open: clr
  Register #(.width(32)) x11_a1 (.D(write_data), .en(decoder_1_out11), .clk(clock_2_out), .Q(x11_a1_q));  // open: clr
  Register #(.width(32)) x4_tp (.D(write_data), .en(decoder_1_out4), .clk(clock_2_out), .Q(x4_tp_q));  // open: clr
  Register #(.width(32)) x12_a2 (.D(write_data), .en(decoder_1_out12), .clk(clock_2_out), .Q(x12_a2_q));  // open: clr
  Clock clock_3 (.out(clock_3_out));
  Register #(.width(32)) x5_t0 (.D(write_data), .en(decoder_1_out5), .clk(clock_2_out), .Q(x5_t0_q));  // open: clr
  Register #(.width(32)) x13_a3 (.D(write_data), .en(decoder_1_out13), .clk(clock_2_out), .Q(x13_a3_q));  // open: clr
  Decoder #(.select(2)) decoder_2 (
    .out0(decoder_2_out0), .out1(decoder_2_out1), .out2(decoder_2_out2), .out3(decoder_2_out3),
    .sel(sb_byte_selector), .en(is_sb));
  Comparator #(.mode("unsigned"), .width(32)) comparator_1 (
    .a(mem_addr), .b(32'h20040000), .lt(comparator_1_lt));  // open: gt, eq
  Comparator #(.mode("unsigned"), .width(32)) comparator_2 (
    .a(mem_addr), .b(32'h20000000), .lt(comparator_2_lt));  // open: gt, eq
  // RGB_Video #(.height(256), .scale(1), .width(256)) rgb_video_1: pin names not known; wires that end beside it: clock_3_out, vga_write, mem_addr[9:2], mem_addr[17:10], vga_color
  Shifter #(.shift("lr"), .width(32)) shifter_2 (.in(mem_addr), .\dist (5'b00010), .out(shifter_2_out));
  Clock clock_4 (.out(clock_4_out));
  Register #(.width(32)) x6_t1 (.D(write_data), .en(decoder_1_out6), .clk(clock_2_out), .Q(x6_t1_q));  // open: clr
  Register #(.width(32)) x14_a4 (.D(write_data), .en(decoder_1_out14), .clk(clock_2_out), .Q(x14_a4_q));  // open: clr
  or or_4 (RAM_BE0, is_sw, decoder_2_out0);
  or or_5 (RAM_BE1, is_sw, decoder_2_out1);
  or or_6 (RAM_BE2, is_sw, decoder_2_out2);
  or or_7 (RAM_BE3, is_sw, decoder_2_out3);
  not not_1 (not_1_out, comparator_2_lt);
  RAM #(.addrWidth(24), .asyncread("true"), .byteenables("byteEnables"), .dataWidth(32)) ram_1 (
    .addr(bit_extender_3_out), .we(RAM_WE), .oe(1'b1), .clk(clock_4_out), .din(mem_data), .dout(RAM_data),
    .be3(RAM_BE3), .be2(RAM_BE2), .be1(RAM_BE1), .be0(RAM_BE0));
  Bit_Extender #(.in_width(32), .out_width(24), .\type ("zero")) bit_extender_3 (
    .in(shifter_2_out), .out(bit_extender_3_out));
  Register #(.width(32)) x7_t2 (.D(write_data), .en(decoder_1_out7), .clk(clock_2_out), .Q(x7_t2_q));  // open: clr
  Register #(.width(32)) x15_a5 (.D(write_data), .en(decoder_1_out15), .clk(clock_2_out), .Q(x15_a5_q));  // open: clr
  and and_3 (is_vga, comparator_1_lt, not_1_out);
  not not_2 (is_ram, is_vga);
  Multiplexer #(.select(4), .width(32)) multiplexer_1 (
    .in0({32{1'b0}}), .in1(x1_ra_q), .in2(x2_sp_q), .in3(x3_gp_q), .in4(x4_tp_q), .in5(x5_t0_q),
    .in6(x6_t1_q), .in7(x7_t2_q), .in8(x8_s0_fp_q), .in9(x9_s1_q), .in10(x10_a0_q), .in11(x11_a1_q),
    .in12(x12_a2_q), .in13(x13_a3_q), .in14(x14_a4_q), .in15(x15_a5_q), .out(rs1_data), .sel(rs1_addr));
  Multiplexer #(.select(4), .width(32)) multiplexer_2 (
    .in0({32{1'b0}}), .in1(x1_ra_q), .in2(x2_sp_q), .in3(x3_gp_q), .in4(x4_tp_q), .in5(x5_t0_q),
    .in6(x6_t1_q), .in7(x7_t2_q), .in8(x8_s0_fp_q), .in9(x9_s1_q), .in10(x10_a0_q), .in11(x11_a1_q),
    .in12(x12_a2_q), .in13(x13_a3_q), .in14(x14_a4_q), .in15(x15_a5_q), .out(rs2_data), .sel(rs2_addr));
  assign bit_extender_4_out = {{20{funct7[6]}}, {funct7, I_Type_imm}};  // Bit_Extender bit_extender_4
  assign bit_extender_5_out = {{20{funct7[6]}}, {funct7, I_Type_imm}};  // Bit_Extender bit_extender_5
  Adder #(.width(32)) adder_1 (.a(rs1_data), .b(rs2_data), .out(adder_1_out));  // open: cin, cout
  assign bit_extender_6_out = {{20{funct7[6]}}, {funct7, operation[11:7]}};  // Bit_Extender bit_extender_6
  assign mem_data = is_sw ? rs2_data : 32'bz;  // Controlled_Buffer controlled_buffer_1
  Adder #(.width(32)) adder_2 (.a(bit_extender_4_out), .b(rs1_data), .out(adder_2_out));  // open: cin, cout
  Adder #(.width(32)) adder_3 (.a(bit_extender_5_out), .b(rs1_data), .out(adder_3_out));  // open: cin, cout
  assign write_data = is_add ? adder_1_out : 32'bz;  // Controlled_Buffer controlled_buffer_2
  Adder #(.width(32)) adder_4 (.a(bit_extender_6_out), .b(rs1_data), .out(adder_4_out));  // open: cin, cout
  assign write_data = is_addi ? adder_2_out : 32'bz;  // Controlled_Buffer controlled_buffer_3
  // NoConnect on adder_3_out[0]
  Adder #(.width(32)) adder_5 (.a(PC_data), .b(32'h1), .out(adder_5_out));  // open: cin, cout
  assign write_data = is_lui ? {funct7, I_Type_imm, operation[19:15], funct3, {12{1'b0}}} : 32'bz;  // Controlled_Buffer controlled_buffer_4
  assign mem_addr = is_sw ? adder_4_out : 32'bz;  // Controlled_Buffer controlled_buffer_5
  Bit_Extender #(.in_width(5), .out_width(4), .\type ("zero")) bit_extender_7 (.in(operation[11:7]), .out(waddr));
  Bit_Extender #(.in_width(5), .out_width(4), .\type ("zero")) bit_extender_8 (.in(operation[19:15]), .out(rs1_addr));
  Bit_Extender #(.in_width(5), .out_width(4), .\type ("zero")) bit_extender_9 (.in(operation[11:7]), .out(waddr));
  Bit_Extender #(.in_width(5), .out_width(4), .\type ("zero")) bit_extender_10 (.in(operation[19:15]), .out(rs1_addr));
  Bit_Extender #(.in_width(5), .out_width(4), .\type ("zero")) bit_extender_11 (.in(I_Type_imm), .out(rs2_addr));
  Bit_Extender #(.in_width(5), .out_width(4), .\type ("zero")) bit_extender_12 (.in(operation[11:7]), .out(waddr));
  Bit_Extender #(.in_width(5), .out_width(4), .\type ("zero")) bit_extender_13 (.in(operation[19:15]), .out(rs1_addr));
  Bit_Extender #(.in_width(5), .out_width(4), .\type ("zero")) bit_extender_14 (.in(I_Type_imm), .out(rs2_addr));
  Shifter #(.shift("lr"), .width(32)) shifter_3 (
    .in({adder_3_out[31:1], 1'b0}), .\dist (5'b00010), .out(shifter_3_out));
  Shifter #(.width(32)) shifter_4 (.in(adder_5_out), .\dist (5'b00010), .out(shifter_4_out));
  assign new_PC_data = is_jalr ? shifter_3_out : 32'bz;  // Controlled_Buffer controlled_buffer_6
  assign write_data = is_jalr ? shifter_4_out : 32'bz;  // Controlled_Buffer controlled_buffer_7
  assign bit_extender_15_out = {{20{funct7[6]}}, {funct7, I_Type_imm}};  // Bit_Extender bit_extender_15
  assign write_data = is_lw ? RAM_data : 32'bz;  // Controlled_Buffer controlled_buffer_8
  assign bit_extender_16_out = {{20{funct7[6]}}, {funct7, I_Type_imm}};  // Bit_Extender bit_extender_16
  assign bit_extender_17_out = {{20{funct7[6]}}, {funct7, operation[11:7]}};  // Bit_Extender bit_extender_17
  Comparator #(.mode("unsigned"), .width(7)) comparator_3 (
    .a(7'b0010011), .b(opcode), .eq(comparator_3_eq));  // open: gt, lt
  Comparator #(.mode("unsigned"), .width(3)) comparator_4 (
    .a(3'b000), .b(funct3), .eq(comparator_4_eq));  // open: gt, lt
  Comparator #(.mode("unsigned"), .width(7)) comparator_5 (
    .a(7'b1100111), .b(opcode), .eq(comparator_5_eq));  // open: gt, lt
  Comparator #(.mode("unsigned"), .width(3)) comparator_6 (
    .a(3'b000), .b(funct3), .eq(comparator_6_eq));  // open: gt, lt
  Comparator #(.mode("unsigned"), .width(7)) comparator_7 (
    .a(7'b0110011), .b(opcode), .eq(comparator_7_eq));  // open: gt, lt
  Comparator #(.mode("unsigned"), .width(3)) comparator_8 (
    .a(3'b000), .b(funct3), .eq(comparator_8_eq));  // open: gt, lt
  Comparator #(.mode("unsigned"), .width(7)) comparator_9 (
    .a({7{1'b0}}), .b(funct7), .eq(comparator_9_eq));  // open: gt, lt
  Comparator #(.mode("unsigned"), .width(7)) comparator_10 (.a(7'b0110111), .b(opcode), .eq(is_lui));  // open: gt, lt
  Comparator #(.mode("unsigned"), .width(7)) comparator_11 (
    .a(7'b0000011), .b(opcode), .eq(comparator_11_eq));  // open: gt, lt
  Comparator #(.mode("unsigned"), .width(3)) comparator_12 (
    .a(3'b010), .b(funct3), .eq(comparator_12_eq));  // open: gt, lt
  Comparator #(.mode("unsigned"), .width(7)) comparator_13 (
    .a(7'b0000011), .b(opcode), .eq(comparator_13_eq));  // open: gt, lt
  Comparator #(.mode("unsigned"), .width(3)) comparator_14 (
    .a(3'b100), .b(funct3), .eq(comparator_14_eq));  // open: gt, lt
  Comparator #(.mode("unsigned"), .width(7)) comparator_15 (
    .a(7'b0100011), .b(opcode), .eq(comparator_15_eq));  // open: gt, lt
  Comparator #(.mode("unsigned"), .width(3)) comparator_16 (
    .a(3'b010), .b(funct3), .eq(comparator_16_eq));  // open: gt, lt
  Comparator #(.mode("unsigned"), .width(7)) comparator_17 (
    .a(7'b0100011), .b(opcode), .eq(comparator_17_eq));  // open: gt, lt
  Comparator #(.mode("unsigned"), .width(3)) comparator_18 (
    .a(3'b000), .b(funct3), .eq(comparator_18_eq));  // open: gt, lt
  Adder #(.width(32)) adder_6 (.a(bit_extender_15_out), .b(rs1_data), .out(adder_6_out));  // open: cin, cout
  Adder #(.width(32)) adder_7 (.a(bit_extender_16_out), .b(rs1_data), .out(adder_7_out));  // open: cin, cout
  Multiplier #(.width(5)) multiplier_1 (
    .a(lbu_byte_selector), .b(5'b01000), .out(multiplier_1_out));  // open: cin, cout
  Adder #(.width(32)) adder_8 (.a(bit_extender_17_out), .b(rs1_data), .out(adder_8_out));  // open: cin, cout
  assign bit_extender_18_out = {{3{1'b0}}, sb_byte_selector};  // Bit_Extender bit_extender_18
  and and_4 (is_addi, comparator_3_eq, comparator_4_eq);
  and and_5 (is_jalr, comparator_5_eq, comparator_6_eq);
  and and_6 (is_add, comparator_7_eq, comparator_8_eq, comparator_9_eq);
  and and_7 (is_lw, comparator_11_eq, comparator_12_eq);
  and and_8 (is_lbu, comparator_13_eq, comparator_14_eq);
  and and_9 (is_sw, comparator_15_eq, comparator_16_eq);
  and and_10 (is_sb, comparator_17_eq, comparator_18_eq);
  assign mem_addr = is_lw ? adder_6_out : 32'bz;  // Controlled_Buffer controlled_buffer_9
  assign mem_addr = is_sb ? adder_8_out : 32'bz;  // Controlled_Buffer controlled_buffer_10
  Multiplier #(.width(5)) multiplier_2 (
    .a(bit_extender_18_out), .b(5'b01000), .out(multiplier_2_out));  // open: cin, cout
  assign mem_addr = is_lbu ? adder_7_out : 32'bz;  // Controlled_Buffer controlled_buffer_11
  assign and_11_out = adder_7_out & 32'h3;  // AND_Gate and_11, 32 bits wide
  Shifter #(.width(32)) shifter_5 (.in(32'hff), .\dist (multiplier_1_out), .out(shifter_5_out));
  assign and_12_out = adder_8_out & 32'h3;  // AND_Gate and_12, 32 bits wide
  Shifter #(.width(32)) shifter_6 (.in(rs2_data), .\dist (multiplier_2_out), .out(shifter_6_out));
  Bit_Extender #(.in_width(32), .out_width(5), .\type ("zero")) bit_extender_19 (
    .in(and_11_out), .out(lbu_byte_selector));
  assign and_13_out = RAM_data & shifter_5_out;  // AND_Gate and_13, 32 bits wide
  Shifter #(.shift("lr"), .width(32)) shifter_7 (.in(and_13_out), .\dist (multiplier_1_out), .out(shifter_7_out));
  Bit_Extender #(.in_width(32), .out_width(2), .\type ("zero")) bit_extender_20 (
    .in(and_12_out), .out(sb_byte_selector));
  assign mem_data = is_sb ? shifter_6_out : 32'bz;  // Controlled_Buffer controlled_buffer_12
  assign write_data = is_lbu ? shifter_7_out : 32'bz;  // Controlled_Buffer controlled_buffer_13

  // Other names for the same wires on the sheet: vga_x[7:0] = mem_addr[9:2]; vga_y[7:0] = mem_addr[17:10];
  //   operation (some bits) = {funct7, I_Type_imm, funct3, opcode}; S_Type_imm[11:0] = {funct7, operation[11:7]};
  //   I_Type_imm[11:5] = funct7; U_Type_imm[31:12] = {funct7, I_Type_imm, operation[19:15], funct3}

  // Notes on the sheet:
  //   contents of rom_1 (hex, n*v repeats v):
  //   413 93137 10113 10b7 dbc08093 80e7 fe012823 fea10923 fea12423 fe914203 fe4109a3 ff012783 f787b3
  //   f787b3 4b6b7 f0068693 fdc10113 d787b3 10000713 f12423 10593 100793 b00513 2112023 12023 12223 e12623
  //   e12823 f10a23 10b7 a8408093 80e7 2012083 2410113 8067 ff410113 112423 10b7 a7c08093 80e7 513 1800093
  //   80e7 812083 513 c10113 8067 852583 feb12823 fe812e23 3437 a0840413 ff014183 3401b3 1c183 ff114203
  //   440233 24203 4181b3 ff214203 440233 24203 4181b3 ff314203 440233 24203 4181b3 3237 a0020213 320233
  //   24203 ffc12403 420233 420233 410233 11b7 85c18193 fe312823 14800193 fe312623 fec22203 20067 1052703
  //   52683 452783 fe810113 e12423 112a23 fed12823 fef12623 13737 c0070713 fe012223 ff314203 fe4102a3
  //   fef14203 fe410223 fe412203 470233 24203 fe4105a3 ff214203 fe4102a3 fee14203 fe410223 fe412203 470233
  //   24203 fe410523 ff114203 fe4102a3 fed14203 fe410223 fe412203 470233 24203 fe4104a3 ff014203 fe4102a3
  //   fec14203 fe410223 fe412203 470233 24203 fe410423 fe812703 c52603 fee12823 fe812e23 3437 a0840413
  //   ff014183 3401b3 1c183 ff114203 440233 24203 4181b3 ff214203 440233 24203 4181b3 ff314203 440233
  //   24203 4181b3 3237 a0020213 320233 24203 ffc12403 420233 420233 410233 66800193 fe312823 28000193
  //   fe312623 fec22203 20067 c68733 10000513 fe812e23 fe912c23 fee12823 50413 ff012483 fe812423 feb14183
  //   3181b3 fe312423 fe914183 3181b3 fe912423 feb14203 420233 fe412423 fe914203 4181b3 3181b3 fe312a23
  //   fe912423 33237 b0020213 feb14183 4181b3 1c183 fe3103a3 fea14183 4181b3 1c183 fe310323 fe914183
  //   4181b3 1c183 fe3102a3 fe814183 4181b3 1c183 fe310223 ff412183 fe412203 440233 120213 fe412423
  //   feb14203 420233 fe412423 fe914203 4181b3 3237 b0820213 320233 ff812483 ffc12403 24203 420233 420233
  //   410233 11b7 86018193 fe312823 38800193 fe312623 fec22203 20067 812703 10000513 812823 e78733
  //   fe812e23 fe912c23 fee12823 50413 ff012483 fe812423 feb14183 3181b3 fe312423 fe914183 3181b3 fe912423
  //   feb14203 420233 fe412423 fe914203 4181b3 3181b3 fe312a23 fe912423 33237 b0020213 feb14183 4181b3
  //   1c183 fe3103a3 fea14183 4181b3 1c183 fe310323 fe914183 4181b3 1c183 fe3102a3 fe814183 4181b3 1c183
  //   fe310223 ff412183 fe412203 440233 120213 fe412423 feb14203 420233 fe412423 fe914203 4181b3 3237
  //   b0820213 320233 ff812483 ffc12403 24203 420233 420233 410233 11b7 86418193 fe312823 49800193
  //   fe312623 fec22203 20067 8*f787b3 d787b3 f787b3 f787b3 20000437 f40433 812783 c60633 c60633 fef12423
  //   feb14183 3181b3 fe312423 fe914183 fff78213 fe412423 feb14203 420233 fe412423 fe914203 4181b3 3237
  //   b1820213 418233 24203 420233 420233 410233 65800193 fe312823 53c00193 fe312623 fec22203 20067 912623
  //   493 40513 c12223 b12023 10b7 de008093 80e7 12583 412603 812783 148493 40040413 c585b3 fef12823
  //   fe912623 fe812e23 fe912c23 4b437 d0040413 ff014183 340233 100193 320023 fec14183 3401b3 18023 24183
  //   ff114483 940233 100493 920023 fed14483 9404b3 48023 24483 9181b3 ff214483 940233 100493 920023
  //   fee14483 9404b3 48023 24483 9181b3 ff314483 940233 100493 920023 fef14483 9404b3 48023 24483 9181b3
  //   3237 a0020213 320233 24203 ff812483 ffc12403 420233 420233 410233 65400193 fe312823 54400193
  //   fe312623 fec22203 20067 c12483 1012403 1412083 1810113 8067 10000713 fec12823 fee12623 fe812e23
  //   fe912c23 4b437 d0040413 ff014183 340233 100193 320023 fec14183 3401b3 18023 24183 ff114483 940233
  //   100493 920023 fed14483 9404b3 48023 24483 9181b3 ff214483 940233 100493 920023 fee14483 9404b3 48023
  //   24483 9181b3 ff314483 940233 100493 920023 fef14483 9404b3 48023 24483 9181b3 3237 a0020213 320233
  //   24203 ff812483 ffc12403 420233 420233 410233 74c00193 fe312823 28000193 fe312623 fec22203 20067
  //   812703 fee12823 fec12623 fe812e23 fe912c23 4b437 d0040413 ff014183 340233 100193 320023 fec14183
  //   3401b3 18023 24183 ff114483 940233 100493 920023 fed14483 9404b3 48023 24483 9181b3 ff214483 940233
  //   100493 920023 fee14483 9404b3 48023 24483 9181b3 ff314483 940233 100493 920023 fef14483 9404b3 48023
  //   24483 9181b3 3237 a0020213 320233 24203 ff812483 ffc12403 420233 420233 410233 11b7 83418193
  //   fe312823 38800193 fe312623 fec22203 20067 1412083 40637 20000537 1810113 1237 de020213 20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
  //   LUI
  //   I-Type
  //   R-Type
  //   U-Type
  //   S-Type
  //   ADDI
  //   JALR
  //   rd 中存储 (PC‘+1)*4
  //   ADD
  //   SW
  //   LW
  //   LBU
  //   SB
endmodule
